// Logisim project 16bit Comparator & Counters.circ as structural Verilog
module comparators (
  input  [3:0] in_1,
  input  [3:0] in_2,
  input  [3:0] in_3,
  input  [3:0] A,
  input  [3:0] in_5,
  input  [3:0] in_6,
  input  [3:0] in_7,
  input  [3:0] B,
  input  [3:0] in_9,
  input  [3:0] in_10,
  input  [3:0] in_11,
  input  [3:0] in_12,
  input  [3:0] in_13,
  input  [3:0] B_2,
  output out_15,
  output A___B,
  output out_17,
  output out_18,
  output out_19,
  output A___B_2,
  output A___B_3,
  output out_22,
  output out_23
);

  wire n7485_1_pin2, n7485_1_pin5, n7485_1_pin6, n7485_1_pin7, n7485_2_pin2, n7485_3_pin5, n7485_3_pin6,
       n7485_3_pin7, n7485_4_pin5, n7485_4_pin6, n7485_4_pin7, n7485_5_pin2, n7485_5_pin5, n7485_5_pin6,
       n7485_5_pin7;

  _7485 u_7485_1 (
    .pin1(B[3]), .pin2(n7485_1_pin2), .pin3(n7485_1_pin2), .pin4(n7485_1_pin2), .pin5(n7485_1_pin5),
    .pin6(n7485_1_pin6), .pin7(n7485_1_pin7), .pin15(A[3]), .pin14(B[2]), .pin13(A[2]), .pin12(A[1]),
    .pin11(B[1]), .pin10(A[0]), .pin9(B[0]));
  _7485 u_7485_2 (
    .pin1(B_2[3]), .pin2(n7485_2_pin2), .pin3(n7485_2_pin2), .pin4(n7485_2_pin2), .pin5(out_19),
    .pin6(A___B_3), .pin7(out_23), .pin15(in_11[3]), .pin14(B_2[2]), .pin13(in_11[2]), .pin12(in_11[1]),
    .pin11(B_2[1]), .pin10(in_11[0]), .pin9(B_2[0]));
  _7485 u_7485_3 (
    .pin1(in_7[3]), .pin2(n7485_1_pin7), .pin3(n7485_1_pin6), .pin4(n7485_1_pin5), .pin5(n7485_3_pin5),
    .pin6(n7485_3_pin6), .pin7(n7485_3_pin7), .pin15(in_3[3]), .pin14(in_7[2]), .pin13(in_3[2]),
    .pin12(in_3[1]), .pin11(in_7[1]), .pin10(in_3[0]), .pin9(in_7[0]));
  LED led_1 (.in(out_19));
  LED led_2 (.in(A___B_3));
  LED led_3 (.in(out_23));
  _7485 u_7485_4 (
    .pin1(in_6[3]), .pin2(n7485_3_pin7), .pin3(n7485_3_pin6), .pin4(n7485_3_pin5), .pin5(n7485_4_pin5),
    .pin6(n7485_4_pin6), .pin7(n7485_4_pin7), .pin15(in_2[3]), .pin14(in_6[2]), .pin13(in_2[2]),
    .pin12(in_2[1]), .pin11(in_6[1]), .pin10(in_2[0]), .pin9(in_6[0]));
  _7485 u_7485_5 (
    .pin1(in_13[3]), .pin2(n7485_5_pin2), .pin3(n7485_5_pin2), .pin4(n7485_5_pin2), .pin5(n7485_5_pin5),
    .pin6(n7485_5_pin6), .pin7(n7485_5_pin7), .pin15(in_10[3]), .pin14(in_13[2]), .pin13(in_10[2]),
    .pin12(in_10[1]), .pin11(in_13[1]), .pin10(in_10[0]), .pin9(in_13[0]));
  _7485 u_7485_6 (
    .pin1(in_5[3]), .pin2(n7485_4_pin7), .pin3(n7485_4_pin6), .pin4(n7485_4_pin5), .pin5(out_15),
    .pin6(A___B), .pin7(out_17), .pin15(in_1[3]), .pin14(in_5[2]), .pin13(in_1[2]), .pin12(in_1[1]),
    .pin11(in_5[1]), .pin10(in_1[0]), .pin9(in_5[0]));
  LED led_4 (.in(out_15));
  LED led_5 (.in(A___B));
  LED led_6 (.in(out_17));
  _7485 u_7485_7 (
    .pin1(in_12[3]), .pin2(n7485_5_pin7), .pin3(n7485_5_pin6), .pin4(n7485_5_pin5), .pin5(out_18),
    .pin6(A___B_2), .pin7(out_22), .pin15(in_9[3]), .pin14(in_12[2]), .pin13(in_9[2]), .pin12(in_9[1]),
    .pin11(in_12[1]), .pin10(in_9[0]), .pin9(in_12[0]));
  LED led_7 (.in(out_18));
  LED led_8 (.in(A___B_2));
  LED led_9 (.in(out_22));
  // also tied to VCC on the sheet: {n7485_1_pin2, n7485_2_pin2, n7485_5_pin2}

  // Notes on the sheet:
  //   LSB
  //   A
  //   4 Bit Comparator
  //   ~~~~~~~~~~~~~~~~~~~~~~~~~~~~~~~~~
  //   ~~~~~~~~~~~~~~~~~~~~~~~~~~~~~~~~~
  //   A is Greater
  //   B is Greater
  //   16 Bit Comparator
  //   ~~~~~~~~~~~~~~~~~~~~~~~~~~~~~~~~~
  //   ~~~~~~~~~~~~~~~~~~~~~~~~~~~~~~~~~
  //   LSB
  //   A
  //   B
  //   MSB
  //   ~~~~~~~~~~~~~~~~~~~~~~~~~~~~~~~~~
  //   8 Bit Comparator
  //   ~~~~~~~~~~~~~~~~~~~~~~~~~~~~~~~~~
  //   MSB
  //   A is Greater
  //   B is Greater
  //   A is Greater
  //   B is Greater
endmodule

module jk_up_counter (
  output MSB,
  output out_2,
  output LSB
);

  wire CLK_out, digital_oscilloscope_1_p5, j_k_ff_1_qn, j_k_ff_2_qn, Reset_out;

  Clock CLK (.out(CLK_out));
  Button Reset (.out(Reset_out));
  J_K_Flip_Flop j_k_ff_1 (
    .J(1'b1), .K(1'b1), .clk(CLK_out), .Q(LSB), .Qn(j_k_ff_1_qn), .reset(Reset_out));  // open: preset
  J_K_Flip_Flop j_k_ff_2 (
    .J(1'b1), .K(1'b1), .clk(j_k_ff_1_qn), .Q(out_2), .Qn(j_k_ff_2_qn), .reset(Reset_out));  // open: preset
  J_K_Flip_Flop j_k_ff_3 (.J(1'b1), .K(1'b1), .clk(j_k_ff_2_qn), .Q(MSB), .reset(Reset_out));  // open: Qn, preset
  LED led_1 (.in(MSB));
  LED led_2 (.in(out_2));
  // Digital_Oscilloscope digital_oscilloscope_1: pin names not known; wires that end beside it: CLK_out, LSB, out_2, MSB, digital_oscilloscope_1_p5
  LED led_3 (.in(LSB));
  Button Clear (.out(digital_oscilloscope_1_p5));

  // Notes on the sheet:
  //   Asynchronous JK Up Counter
  //   ~ ~ ~ ~ ~ ~ ~ ~ ~ ~ ~ ~ ~ ~ ~ ~ ~ ~ ~ ~ ~ ~ ~ ~ ~ ~ ~ ~ ~
  //   ~ ~ ~ ~ ~ ~ ~ ~ ~ ~ ~ ~ ~ ~ ~ ~ ~ ~ ~ ~ ~ ~ ~ ~ ~ ~ ~ ~ ~
endmodule

module D_up_counter (
  output MSB,
  output out_2,
  output LSB
);

  wire clock_1_out, d_ff_1_qn, d_ff_2_qn, d_ff_3_qn;

  D_Flip_Flop d_ff_1 (.D(d_ff_1_qn), .clk(clock_1_out), .Q(LSB), .Qn(d_ff_1_qn));  // open: preset, reset
  Clock clock_1 (.out(clock_1_out));
  D_Flip_Flop d_ff_2 (.D(d_ff_2_qn), .clk(d_ff_1_qn), .Q(out_2), .Qn(d_ff_2_qn));  // open: preset, reset
  // Digital_Oscilloscope digital_oscilloscope_1: pin names not known; wires that end beside it: clock_1_out, LSB, out_2, MSB, d_ff_2_qn
  D_Flip_Flop d_ff_3 (.D(d_ff_3_qn), .clk(d_ff_2_qn), .Q(MSB), .Qn(d_ff_3_qn));  // open: preset, reset
  LED led_1 (.in(MSB));
  LED led_2 (.in(out_2));
  LED led_3 (.in(LSB));

  // Notes on the sheet:
  //   Asynchronous D Up Counter
endmodule

module JK_down_counter (
  input  in_1,
  input  Clear,
  output MSB,
  output out_4,
  output LSB
);

  wire CLK_out;

  J_K_Flip_Flop j_k_ff_1 (.J(1'b1), .K(1'b1), .clk(CLK_out), .Q(LSB), .reset(in_1));  // open: Qn, preset
  Clock CLK (.out(CLK_out));
  J_K_Flip_Flop j_k_ff_2 (.J(1'b1), .K(1'b1), .clk(LSB), .Q(out_4), .reset(in_1));  // open: Qn, preset
  J_K_Flip_Flop j_k_ff_3 (.J(1'b1), .K(1'b1), .clk(out_4), .Q(MSB), .reset(in_1));  // open: Qn, preset
  LED led_1 (.in(MSB));
  // Digital_Oscilloscope digital_oscilloscope_1: pin names not known; wires that end beside it: CLK_out, LSB, out_4, MSB, Clear
  LED led_2 (.in(out_4));
  LED led_3 (.in(LSB));

  // Notes on the sheet:
  //   Asynchronous JK Down Counter
  //   ~ ~ ~ ~ ~ ~ ~ ~ ~ ~ ~ ~ ~ ~ ~ ~ ~ ~ ~ ~ ~ ~ ~ ~ ~ ~ ~ ~ ~
  //   ~ ~ ~ ~ ~ ~ ~ ~ ~ ~ ~ ~ ~ ~ ~ ~ ~ ~ ~ ~ ~ ~ ~ ~ ~ ~ ~ ~ ~
endmodule

module D_down_counter (
  output LSB,
  output out_2,
  output MSB
);

  wire CLK_out, d_ff_1_qn, d_ff_2_qn, d_ff_3_qn;

  Clock CLK (.out(CLK_out));
  D_Flip_Flop d_ff_1 (.D(d_ff_1_qn), .clk(CLK_out), .Q(LSB), .Qn(d_ff_1_qn));  // open: preset, reset
  D_Flip_Flop d_ff_2 (.D(d_ff_2_qn), .clk(LSB), .Q(out_2), .Qn(d_ff_2_qn));  // open: preset, reset
  D_Flip_Flop d_ff_3 (.D(d_ff_3_qn), .clk(out_2), .Q(MSB), .Qn(d_ff_3_qn));  // open: preset, reset
  LED led_1 (.in(LSB));
  LED led_2 (.in(out_2));
  LED led_3 (.in(MSB));

  // Notes on the sheet:
  //   Asynchronous D Down Counter
endmodule
