// Logisim project 3-bit Multiplier and Ring & Johnson Counters.circ as structural Verilog: 3 circuits, main circuit Multiplier_3bit
module Multiplier_3bit (
  input  [2:0] A,
  input  [2:0] B,
  output P5,
  output P4,
  output P3,
  output P2,
  output P1,
  output P0
);

  wire [1:0] and_2_out;
  wire [2:0] and_4_out, and_7_out;
  wire [2:1] adder_1_out;
  wire [2:2] adder_1_cout;

  and and_1 (P0, A[0], B[0]);
  and and_2 (and_2_out[0], A[1], B[0]);
  and and_3 (and_2_out[1], A[2], B[0]);
  and and_4 (and_4_out[0], A[0], B[1]);
  and and_5 (and_4_out[1], A[1], B[1]);
  and and_6 (and_4_out[2], A[2], B[1]);
  Adder #(.width(3)) adder_1 (
    .a({1'b0, and_2_out}), .b(and_4_out), .out({adder_1_out, P1}), .cout(adder_1_cout[2]));  // open: cin
  and and_7 (and_7_out[0], A[0], B[2]);
  and and_8 (and_7_out[1], B[2], A[1]);
  and and_9 (and_7_out[2], B[2], A[2]);
  Adder #(.width(3)) adder_2 (
    .a({adder_1_cout[2], adder_1_out}), .b(and_7_out), .out({P4, P3, P2}), .cout(P5));  // open: cin
  LED led_1 (.in(P5));
  LED led_2 (.in(P4));
  LED led_3 (.in(P3));
  LED led_4 (.in(P2));
  LED led_5 (.in(P1));
  LED led_6 (.in(P0));

  // Notes on the sheet:
  //   3-bit Multiplier
endmodule

module Ring_Counter (
  output Q0,
  output Q1,
  output Q2,
  output Q3,
  output Q4
);

  wire Clk_out, Reset_out;

  Button Reset (.out(Reset_out));
  Clock Clk (.out(Clk_out));
  D_Flip_Flop d_ff_1 (.D(Q4), .clk(Clk_out), .Q(Q0), .reset(Reset_out));  // open: Qn, preset
  D_Flip_Flop d_ff_2 (.D(Q0), .clk(Clk_out), .Q(Q1), .reset(Reset_out));  // open: Qn, preset
  LED led_1 (.in(Q0));
  D_Flip_Flop d_ff_3 (.D(Q1), .clk(Clk_out), .Q(Q2), .reset(Reset_out));  // open: Qn, preset
  LED led_2 (.in(Q1));
  D_Flip_Flop d_ff_4 (.D(Q2), .clk(Clk_out), .Q(Q3), .reset(Reset_out));  // open: Qn, preset
  LED led_3 (.in(Q2));
  D_Flip_Flop d_ff_5 (.D(Q3), .clk(Clk_out), .Q(Q4), .reset(Reset_out));  // open: Qn, preset
  LED led_4 (.in(Q3));
  LED led_5 (.in(Q4));

  // Notes on the sheet:
  //   5-bit Ring Counter
endmodule

module Johnson_Counter (
  output Q0,
  output Q1,
  output Q2,
  output Q3,
  output Q4
);

  wire Clk_out, d_ff_5_qn, Reset_out;

  D_Flip_Flop d_ff_1 (.D(d_ff_5_qn), .clk(Clk_out), .Q(Q0), .reset(Reset_out));  // open: Qn, preset
  Button Reset (.out(Reset_out));
  Clock Clk (.out(Clk_out));
  LED led_1 (.in(Q0));
  D_Flip_Flop d_ff_2 (.D(Q0), .clk(Clk_out), .Q(Q1), .reset(Reset_out));  // open: Qn, preset
  LED led_2 (.in(Q1));
  D_Flip_Flop d_ff_3 (.D(Q1), .clk(Clk_out), .Q(Q2), .reset(Reset_out));  // open: Qn, preset
  D_Flip_Flop d_ff_4 (.D(Q2), .clk(Clk_out), .Q(Q3), .reset(Reset_out));  // open: Qn, preset
  LED led_3 (.in(Q2));
  D_Flip_Flop d_ff_5 (.D(Q3), .clk(Clk_out), .Q(Q4), .Qn(d_ff_5_qn), .reset(Reset_out));  // open: preset
  LED led_4 (.in(Q3));
  LED led_5 (.in(Q4));

  // Notes on the sheet:
  //   5-bit Johnson Counter
endmodule
