// Logisim project 4_Circuits_using_NOR_and_NAND.circ as structural Verilog: 1 circuit, main circuit main
module main (
  input  A,
  input  A_2,
  input  B,
  input  B_2,
  input  A_3,
  input  A_4,
  input  B_3,
  input  B_4,
  output out_9,
  output out_10,
  output out_11,
  output out_12
);

  wire nand_1_out, nand_2_out, nand_3_out, nor_1_out, nor_2_out, nor_3_out, nor_6_out, nor_7_out, nor_8_out,
       nor_9_out;

  nor nor_1 (nor_1_out, A, B);
  nor nor_2 (nor_2_out, A_4, A_4);
  nor nor_3 (nor_3_out, B_4, B_4);
  nor nor_4 (out_9, nor_1_out, nor_1_out);
  nor nor_5 (out_12, nor_2_out, nor_3_out);
  nor nor_6 (nor_6_out, A_2, B_2);
  nand nand_1 (nand_1_out, A_3, B_3);
  nor nor_7 (nor_7_out, A_2, nor_6_out);
  nor nor_8 (nor_8_out, nor_6_out, B_2);
  nand nand_2 (nand_2_out, A_3, nand_1_out);
  nand nand_3 (nand_3_out, nand_1_out, B_3);
  nor nor_9 (nor_9_out, nor_7_out, nor_8_out);
  nand nand_4 (out_11, nand_2_out, nand_3_out);
  nor nor_10 (out_10, nor_9_out, nor_9_out);

  // Notes on the sheet:
  //   Using NOR
  //   OR Gate
  //   AND Gate
  //   Using NOR
  //   Using NAND
  //   Using NOR
  //   XOR Gate
  //   XOR Gate
endmodule
