// Logisim project ALU.circ as structural Verilog: 1 circuit, main circuit main
module main (
  input  [2:0] F2_F1_F0,
  input  A,
  input  B,
  input  C,
  output Y1,
  output Y0,
  output out_7,
  output out_8,
  output out_9,
  output out_10
);

  wire xor_1_out, xor_2_out;

  Multiplexer multiplexer_1 (.in0(1'b0), .in1(B), .out(out_7), .sel(A));
  Multiplexer multiplexer_2 (.in0(B), .in1(1'b0), .out(out_8), .sel(A));
  Multiplexer multiplexer_3 (.in0(B), .in1(1'b1), .out(out_9), .sel(A));
  Multiplexer multiplexer_4 (.in0(1'b1), .in1(B), .out(out_10), .sel(A));
  xor xor_1 (xor_1_out, A, B);
  LED led_1 (.in(out_7));
  LED led_2 (.in(out_8));
  LED led_3 (.in(out_9));
  Multiplexer #(.enable("true"), .select(3)) multiplexer_5 (
    .in0(out_7), .in1(out_7), .in2(out_8), .in3(out_8), .in4(out_7), .in5(out_9), .in6(out_8), .in7(out_10),
    .out(Y1), .sel({F2_F1_F0[1:0], C}), .en(F2_F1_F0[2]));
  xor xor_2 (xor_2_out, xor_1_out, C);
  LED led_4 (.in(out_10));
  Multiplexer #(.select(3)) multiplexer_6 (
    .in0(1'b0), .in1(out_9), .in2(out_7), .in3(xor_1_out), .in4(xor_1_out), .in5(xor_1_out), .in6(xor_2_out),
    .in7(xor_2_out), .out(Y0), .sel(F2_F1_F0));
  LED led_5 (.in(Y1));
  LED led_6 (.in(Y0));

  // Notes on the sheet:
  //   MUX
  //   MUX
  //   MUX
  //   MUX
  //   A • B
  //   A’• B
  //   1- Bit ALU
  //   ~ ~ ~ ~ ~ ~ ~ ~ ~ ~ ~ ~ ~ ~ ~ ~
  //   ~ ~ ~ ~ ~ ~ ~ ~ ~ ~ ~ ~ ~ ~ ~ ~
  //   A + B
  //   MUX
  //   A’+ B
  //   MUX
  //   0 0 0
  //   0 1 0
  //   0 1 1
  //   1 0 0
  //   1 0 1
  //   1 1 0
  //   1 1 1
  //   F2 F1 F0
  //   0 0 1
  //   ALU Function
  //   0 (Zero)
  //   A OR B
  //   A AND B
  //   A EXOR B
  //   A PLUS B
  //   A MINUS B
  //   A PLUS B PLUS C
  //   A MINUS B MINUS C
  //   Y1 
  //   -
  //   -
  //   -
  //   -
  //   Carry
  //   Borrow
  //   Carry
  //   Borrow
  //   Y0
  //   0
  //   A + B
  //   A • B
  //   A ⊕ B
  //   Sum
  //   Difference
  //   Sum
  //   Difference
endmodule
