// Logisim project Adder_and_Subtractor.circ as structural Verilog: 1 circuit, main circuit main
module main (
  input  Input_A,
  input  Input_B,
  input  Enabler_for_Subtraction,
  output [1:0] Sum,
  output Difference,
  output Borrow
);

  wire and_1_out, and_2_out, and_5_out, bcd_to_7_segment_decoder_1_p1, bcd_to_7_segment_decoder_1_p2,
       bcd_to_7_segment_decoder_1_p3, bcd_to_7_segment_decoder_1_p4, bcd_to_7_segment_decoder_1_p6,
       bcd_to_7_segment_decoder_1_p7, bcd_to_7_segment_decoder_1_p8, bcd_to_7_segment_decoder_2_p1,
       bcd_to_7_segment_decoder_2_p2, bcd_to_7_segment_decoder_2_p3, bcd_to_7_segment_decoder_2_p4,
       bcd_to_7_segment_decoder_2_p6, bcd_to_7_segment_decoder_2_p7, bcd_to_7_segment_decoder_2_p8,
       bcd_to_7_segment_decoder_3_p1, bcd_to_7_segment_decoder_3_p2, bcd_to_7_segment_decoder_3_p3,
       bcd_to_7_segment_decoder_3_p4, bcd_to_7_segment_decoder_3_p6, bcd_to_7_segment_decoder_3_p7,
       bcd_to_7_segment_decoder_3_p8, bcd_to_7_segment_decoder_4_p1, bcd_to_7_segment_decoder_4_p2,
       bcd_to_7_segment_decoder_4_p3, bcd_to_7_segment_decoder_4_p4, bcd_to_7_segment_decoder_4_p6,
       bcd_to_7_segment_decoder_4_p7, bcd_to_7_segment_decoder_4_p8, bcd_to_7_segment_decoder_5_p1,
       bcd_to_7_segment_decoder_5_p2, bcd_to_7_segment_decoder_5_p3, bcd_to_7_segment_decoder_5_p4,
       bcd_to_7_segment_decoder_5_p6, bcd_to_7_segment_decoder_5_p7, bcd_to_7_segment_decoder_5_p8;

  // BCD_to_7_Segment_decoder bcd_to_7_segment_decoder_1: pin names not known; wires that end beside it: bcd_to_7_segment_decoder_1_p1, bcd_to_7_segment_decoder_1_p2, bcd_to_7_segment_decoder_1_p3, bcd_to_7_segment_decoder_1_p4, {3'b000, Input_B}, bcd_to_7_segment_decoder_1_p6, bcd_to_7_segment_decoder_1_p7, bcd_to_7_segment_decoder_1_p8
  // BCD_to_7_Segment_decoder bcd_to_7_segment_decoder_2: pin names not known; wires that end beside it: bcd_to_7_segment_decoder_2_p1, bcd_to_7_segment_decoder_2_p2, bcd_to_7_segment_decoder_2_p3, bcd_to_7_segment_decoder_2_p4, {3'b000, Input_A}, bcd_to_7_segment_decoder_2_p6, bcd_to_7_segment_decoder_2_p7, bcd_to_7_segment_decoder_2_p8
  _7_Segment_Display u_7_segment_display_1 (
    .g(bcd_to_7_segment_decoder_2_p1), .f(bcd_to_7_segment_decoder_2_p3), .a(bcd_to_7_segment_decoder_2_p6),
    .b(bcd_to_7_segment_decoder_2_p8), .e(bcd_to_7_segment_decoder_2_p2), .d(bcd_to_7_segment_decoder_2_p4),
    .c(bcd_to_7_segment_decoder_2_p7));  // open: dp
  _7_Segment_Display u_7_segment_display_2 (
    .g(bcd_to_7_segment_decoder_1_p1), .f(bcd_to_7_segment_decoder_1_p3), .a(bcd_to_7_segment_decoder_1_p6),
    .b(bcd_to_7_segment_decoder_1_p8), .e(bcd_to_7_segment_decoder_1_p2), .d(bcd_to_7_segment_decoder_1_p4),
    .c(bcd_to_7_segment_decoder_1_p7));  // open: dp
  and and_1 (and_1_out, ~Input_A, Input_B, ~Enabler_for_Subtraction);  // AND_Gate
  and and_2 (and_2_out, Input_A, ~Input_B, ~Enabler_for_Subtraction);  // AND_Gate
  and and_3 (Sum[1], Input_A, Input_B, ~Enabler_for_Subtraction);  // AND_Gate
  and and_4 (Borrow, ~Input_A, Input_B, Enabler_for_Subtraction);  // AND_Gate
  and and_5 (and_5_out, Input_A, ~Input_B, Enabler_for_Subtraction);  // AND_Gate
  or or_1 (Sum[0], and_1_out, and_2_out);
  or or_2 (Difference, Borrow, and_5_out);
  // BCD_to_7_Segment_decoder bcd_to_7_segment_decoder_3: pin names not known; wires that end beside it: bcd_to_7_segment_decoder_3_p1, bcd_to_7_segment_decoder_3_p2, bcd_to_7_segment_decoder_3_p3, bcd_to_7_segment_decoder_3_p4, {2'b00, Sum}, bcd_to_7_segment_decoder_3_p6, bcd_to_7_segment_decoder_3_p7, bcd_to_7_segment_decoder_3_p8
  // BCD_to_7_Segment_decoder bcd_to_7_segment_decoder_4: pin names not known; wires that end beside it: bcd_to_7_segment_decoder_4_p1, bcd_to_7_segment_decoder_4_p2, bcd_to_7_segment_decoder_4_p3, bcd_to_7_segment_decoder_4_p4, {3'b000, Difference}, bcd_to_7_segment_decoder_4_p6, bcd_to_7_segment_decoder_4_p7, bcd_to_7_segment_decoder_4_p8
  _7_Segment_Display u_7_segment_display_3 (
    .g(bcd_to_7_segment_decoder_3_p1), .f(bcd_to_7_segment_decoder_3_p3), .a(bcd_to_7_segment_decoder_3_p6),
    .b(bcd_to_7_segment_decoder_3_p8), .e(bcd_to_7_segment_decoder_3_p2), .d(bcd_to_7_segment_decoder_3_p4),
    .c(bcd_to_7_segment_decoder_3_p7));  // open: dp
  _7_Segment_Display u_7_segment_display_4 (
    .g(bcd_to_7_segment_decoder_4_p1), .f(bcd_to_7_segment_decoder_4_p3), .a(bcd_to_7_segment_decoder_4_p6),
    .b(bcd_to_7_segment_decoder_4_p8), .e(bcd_to_7_segment_decoder_4_p2), .d(bcd_to_7_segment_decoder_4_p4),
    .c(bcd_to_7_segment_decoder_4_p7));  // open: dp
  // BCD_to_7_Segment_decoder bcd_to_7_segment_decoder_5: pin names not known; wires that end beside it: bcd_to_7_segment_decoder_5_p1, bcd_to_7_segment_decoder_5_p2, bcd_to_7_segment_decoder_5_p3, bcd_to_7_segment_decoder_5_p4, {3'b000, Borrow}, bcd_to_7_segment_decoder_5_p6, bcd_to_7_segment_decoder_5_p7, bcd_to_7_segment_decoder_5_p8
  _7_Segment_Display u_7_segment_display_5 (
    .g(bcd_to_7_segment_decoder_5_p1), .f(bcd_to_7_segment_decoder_5_p3), .a(bcd_to_7_segment_decoder_5_p6),
    .b(bcd_to_7_segment_decoder_5_p8), .e(bcd_to_7_segment_decoder_5_p2), .d(bcd_to_7_segment_decoder_5_p4),
    .c(bcd_to_7_segment_decoder_5_p7));  // open: dp

  // Notes on the sheet:
  //   /
  //   + / -
  //   /
  //   1- bit Adder & Subtractor 
  //   |
  //   ____________
  //   |
  //   |
  //   |
  //   |
  //   |
  //   Addition
  //   ________________________
  //   A + B
  //   Subtraction
  //   ________________________
  //   A - B
  //   >
  //   >
  //   Borrow
endmodule
