// Logisim project Circuit_3.circ as structural Verilog: 1 circuit, main circuit main
module main (
  input  X,
  input  Z,
  input  Y,
  input  z_2,
  output out_5,
  output nz
);

  wire and_1_out, and_2_out, and_3_out, not_1_out, not_2_out, or_1_out;

  and and_1 (and_1_out, X, Z);
  not not_1 (not_1_out, Y);
  not not_2 (not_2_out, X);
  and and_2 (and_2_out, Z, not_1_out);
  and and_3 (and_3_out, not_2_out, Z, Y);
  not not_3 (nz, z_2);
  or or_1 (or_1_out, and_1_out, and_2_out, and_3_out);
  not not_4 (out_5, or_1_out);

  // Notes on the sheet:
  //   Circuit 3
  //   XZ
  //   {OR}
  //   ~YZ
  //   ~XYZ
  //   ~[(XZ)+(~YZ)+(~XYZ)]
  //   =Z(1+X)
  //   =Z
  //   Y=(XZ)+(~YZ)+(~XYZ)
  //   =Z(X+ ~Y+ ~XY)
  //   =Z(X+ ~Y+Y)
endmodule
