// Logisim project BCD to 7-Segment(Hexa_Decimal).circ as structural Verilog
module BCD (
  input  A,
  input  B,
  input  C,
  input  D,
  output a_2,
  output b_2,
  output c_2,
  output d_2,
  output e,
  output f,
  output g
);

  wire and_1_out, and_2_out, and_3_out, and_4_out, and_5_out, and_6_out, and_7_out, and_8_out, and_9_out,
       and_10_out, and_11_out, and_12_out, and_13_out, and_14_out, and_15_out, and_16_out, and_17_out,
       and_18_out, and_19_out, and_20_out, and_21_out, and_22_out, and_23_out, and_24_out, and_25_out,
       and_26_out, and_27_out, and_28_out, and_29_out, and_30_out, and_31_out, and_32_out, and_33_out,
       and_34_out, and_35_out, and_36_out, not_1_out, not_2_out, not_3_out, not_4_out;

  not not_1 (not_1_out, A);
  not not_2 (not_2_out, B);
  not not_3 (not_3_out, C);
  not not_4 (not_4_out, D);
  and and_1 (and_1_out, not_2_out, not_4_out);
  and and_2 (and_2_out, not_1_out, C);
  and and_3 (and_3_out, not_1_out, B, D);
  and and_4 (and_4_out, B, C);
  and and_5 (and_5_out, A, not_2_out, not_3_out);
  and and_6 (and_6_out, A, not_4_out);
  and and_7 (and_7_out, not_1_out, not_2_out);
  and and_8 (and_8_out, not_1_out, not_3_out, not_4_out);
  and and_9 (and_9_out, not_2_out, not_4_out);
  and and_10 (and_10_out, not_1_out, C, D);
  and and_11 (and_11_out, A, not_3_out, D);
  and and_12 (and_12_out, not_1_out, not_3_out);
  and and_13 (and_13_out, not_1_out, D);
  and and_14 (and_14_out, not_3_out, D);
  and and_15 (and_15_out, not_1_out, B);
  and and_16 (and_16_out, A, not_2_out);
  and and_17 (and_17_out, not_1_out, not_2_out, not_4_out);
  and and_18 (and_18_out, not_1_out, C, not_4_out);
  and and_19 (and_19_out, not_2_out, C, D);
  and and_20 (and_20_out, B, not_3_out, D);
  and and_21 (and_21_out, B, C, not_4_out);
  and and_22 (and_22_out, A, not_3_out, not_4_out);
  and and_23 (and_23_out, not_2_out, not_4_out);
  and and_24 (and_24_out, C, not_4_out);
  and and_25 (and_25_out, A, C);
  and and_26 (and_26_out, A, B);
  and and_27 (and_27_out, not_3_out, not_4_out);
  and and_28 (and_28_out, not_1_out, B, not_3_out);
  and and_29 (and_29_out, B, not_4_out);
  and and_30 (and_30_out, A, not_2_out);
  and and_31 (and_31_out, A, C);
  and and_32 (and_32_out, not_2_out, C);
  and and_33 (and_33_out, C, not_4_out);
  and and_34 (and_34_out, not_1_out, B, not_3_out);
  and and_35 (and_35_out, A, not_2_out);
  and and_36 (and_36_out, A, D);
  or or_1 (a_2, and_1_out, and_2_out, and_3_out, and_4_out, and_5_out, and_6_out);
  or or_2 (b_2, and_7_out, and_8_out, and_9_out, and_10_out, and_11_out);
  or or_3 (c_2, and_12_out, and_13_out, and_14_out, and_15_out, and_16_out);
  or or_4 (d_2, and_17_out, and_18_out, and_19_out, and_20_out, and_21_out, and_22_out);
  or or_5 (e, and_23_out, and_24_out, and_25_out, and_26_out);
  or or_6 (f, and_27_out, and_28_out, and_29_out, and_30_out, and_31_out);
  or or_7 (g, and_32_out, and_33_out, and_34_out, and_35_out, and_36_out);
  LED led_1 (.in(a_2));
  LED led_2 (.in(b_2));
  LED led_3 (.in(c_2));
  LED led_4 (.in(d_2));
  LED led_5 (.in(e));
  LED led_6 (.in(f));
  LED led_7 (.in(g));
  _7_Segment_Display u_7_segment_display_1 (.g(g), .f(f), .a(a_2), .b(b_2), .e(e), .d(d_2), .c(c_2));  // open: dp

  // Notes on the sheet:
  //   Circuit Diagram
  //   ~~~~~~~~~~~~~~~~~
  //   ~~~~~~~~~~~~~~~~~
endmodule

module segment (
  input  [3:0] D
);

  wire bcd_1_a_2, bcd_1_b_2, bcd_1_c_2, bcd_1_d_2, bcd_1_e, bcd_1_f, bcd_1_g;

  BCD bcd_1 (
    .A(D[3]), .B(D[2]), .C(D[1]), .D(D[0]), .a_2(bcd_1_a_2), .b_2(bcd_1_b_2), .c_2(bcd_1_c_2),
    .d_2(bcd_1_d_2), .e(bcd_1_e), .f(bcd_1_f), .g(bcd_1_g));
  _7_Segment_Display u_7_segment_display_1 (
    .g(bcd_1_g), .f(bcd_1_f), .a(bcd_1_a_2), .b(bcd_1_b_2), .e(bcd_1_e), .d(bcd_1_d_2), .c(bcd_1_c_2));  // open: dp

  // Notes on the sheet:
  //   A
  //   B
  //   C
  //   A
  //   _______________________________
  //   BCD to 7- Segment
  //   _______________________________
  //   b
  //   c
  //   d
endmodule
