// Logisim project Circuit_4.circ as structural Verilog: 1 circuit, main circuit main
module main (
  input  Y,
  input  X,
  input  Z,
  output out_4
);

  wire and_1_out, not_1_out, not_2_out, or_1_out, or_2_out, or_3_out;

  not not_1 (not_1_out, Y);
  not not_2 (not_2_out, X);
  or or_1 (or_1_out, X, Z);
  or or_2 (or_2_out, not_1_out, Z);
  or or_3 (or_3_out, Y, not_2_out, Z);
  and and_1 (and_1_out, or_3_out, or_2_out, or_1_out);
  not not_3 (out_4, and_1_out);

  // Notes on the sheet:
  //   Circuit 4
  //   ~X+Y+Z
  //   ~Y+Z
  //   X+Z
  //   (X+Z)(~Y+Z)(~X+Y+Z)
  //   ~[(X+Z)(~Y+Z)(~X+Y+Z)]
endmodule
