// Logisim project Decoders & Encoders.circ as structural Verilog: 5 circuits, main circuit main
module main (
  input  EN,
  input  EN_2,
  input  [1:0] B,
  input  [2:0] in_4,
  input  in_5,
  input  in_6,
  input  in_7,
  input  in_8,
  input  in_9,
  input  in_10,
  input  in_11,
  input  in_12,
  input  in_13,
  input  EN_3,
  input  [3:0] A,
  output Y0,
  output Y1,
  output Y0_2,
  output Y2,
  output Y1_2,
  output Y3,
  output Y2_2,
  output Y4,
  output Y5,
  output Y3_2,
  output Y6,
  output Y7,
  output Y6_2,
  output Y9,
  output out_30,
  output Y5_2,
  output Y10,
  output Y3_3,
  output Y12,
  output [2:0] out_35,
  output Y14,
  output out_37,
  output Y1_3,
  output Y15,
  output Y0_3,
  output Y4_2,
  output Y11,
  output out_43,
  output out_44,
  output out_45,
  output out_46
);

  Decoder #(.select(3)) decoder_1 (
    .out0(Y0), .out1(Y1), .out2(Y2), .out3(Y3), .out4(Y4), .out5(Y5), .out6(Y6), .out7(Y7), .sel(in_4),
    .en(EN_2));
  Decoder #(.select(4)) decoder_2 (
    .out0(out_46), .out1(out_44), .out2(Y0_3), .out3(Y1_3), .out4(Y4_2), .out5(Y3_3), .out6(Y5_2),
    .out7(Y6_2), .out8(Y9), .out9(Y10), .out10(Y12), .out11(Y11), .out12(Y14), .out13(Y15), .out14(out_43),
    .out15(out_45), .sel(A), .en(EN_3));
  Decoder #(.select(2)) decoder_3 (.out0(Y0_2), .out1(Y1_2), .out2(Y2_2), .out3(Y3_2), .sel(B), .en(EN));
  Priority_Encoder priority_encoder_1 (
    .in0(in_5), .in1(in_6), .in2(in_7), .in3(in_8), .in4(in_9), .in5(in_10), .in6(in_11), .in7(in_12),
    .out(out_35), .en_in(in_13), .gs(out_37), .en_out(out_30));

  // Notes on the sheet:
  //   Y2
  //   Y8
  //   Y7
  //   B
  //   C D
  //   Y13
  //   A
endmodule

module Decoder3x8 (
  input  EN,
  input  A,
  input  B,
  input  C,
  output Y7,
  output Y6,
  output Y5,
  output Y4,
  output Y3,
  output Y2,
  output Y1,
  output Y0
);

  wire not_1_out, not_2_out, not_3_out;

  not not_1 (not_1_out, A);
  not not_2 (not_2_out, B);
  not not_3 (not_3_out, C);
  and and_1 (Y7, EN, A, B, C);
  and and_2 (Y6, EN, A, B, not_3_out);
  and and_3 (Y5, EN, A, not_2_out, C);
  and and_4 (Y4, EN, A, not_2_out, not_3_out);
  and and_5 (Y3, EN, not_1_out, B, C);
  and and_6 (Y2, EN, not_1_out, B, not_3_out);
  and and_7 (Y1, EN, not_1_out, not_2_out, C);
  and and_8 (Y0, EN, not_1_out, not_2_out, not_3_out);

  // Notes on the sheet:
  //   Decoder 3 X 8
  //   _____________________________
  //   _____________________________
endmodule

module Decoder4x16 (
  input  EN,
  input  A,
  input  B,
  input  C,
  input  D,
  output Y15,
  output Y14,
  output Y13,
  output Y12,
  output Y11,
  output Y10,
  output Y9,
  output Y8,
  output Y7,
  output Y6,
  output Y5,
  output Y4,
  output Y3,
  output Y2,
  output Y1,
  output Y0
);

  wire not_1_out, not_2_out, not_3_out, not_4_out;

  not not_1 (not_1_out, A);
  not not_2 (not_2_out, B);
  not not_3 (not_3_out, C);
  not not_4 (not_4_out, D);
  and and_1 (Y15, EN, A, B, C, D);
  and and_2 (Y14, EN, A, B, C, not_4_out);
  and and_3 (Y13, EN, A, B, not_3_out, D);
  and and_4 (Y12, EN, A, B, not_3_out, not_4_out);
  and and_5 (Y11, EN, A, not_2_out, C, D);
  and and_6 (Y10, EN, A, not_2_out, C, not_4_out);
  and and_7 (Y9, EN, A, not_2_out, not_3_out, D);
  and and_8 (Y8, EN, A, not_2_out, not_3_out, not_4_out);
  and and_9 (Y7, EN, not_1_out, B, C, D);
  and and_10 (Y6, EN, not_1_out, B, C, not_4_out);
  and and_11 (Y5, EN, not_1_out, B, not_3_out, D);
  and and_12 (Y4, EN, not_1_out, B, not_3_out, not_4_out);
  and and_13 (Y3, EN, not_1_out, not_2_out, C, D);
  and and_14 (Y2, EN, not_1_out, not_2_out, C, not_4_out);
  and and_15 (Y1, EN, not_1_out, not_2_out, not_3_out, D);
  and and_16 (Y0, EN, not_1_out, not_2_out, not_3_out, not_4_out);

  // Notes on the sheet:
  //   Decoder 4 X 16
  //   _____________________________
  //   _____________________________
endmodule

module Decoder2x4 (
  input  EN,
  input  A,
  input  B,
  output Y0,
  output Y1,
  output Y2,
  output Y3
);

  wire not_1_out, not_2_out;

  not not_1 (not_1_out, A);
  not not_2 (not_2_out, B);
  and and_1 (Y0, EN, not_1_out, not_2_out);
  and and_2 (Y1, EN, not_1_out, B);
  and and_3 (Y2, EN, A, not_2_out);
  and and_4 (Y3, EN, A, B);

  // Notes on the sheet:
  //   Decoder 2 X 4
  //   _____________________________
  //   _____________________________
endmodule

module Encoder8x3 (
  input  Y0,
  input  Y1,
  input  Y2,
  input  Y3,
  input  Y4,
  input  Y5,
  input  Y6,
  input  Y7,
  output A,
  output B,
  output C
);

  wire or_1_out, or_2_out, or_3_out;

  or or_1 (or_1_out, Y1, Y3, Y5, Y7);
  or or_2 (or_2_out, Y2, Y3, Y6, Y7);
  or or_3 (or_3_out, Y4, Y5, Y6, Y7);
  and and_1 (A, Y0, or_1_out);
  and and_2 (B, Y0, or_2_out);
  and and_3 (C, Y0, or_3_out);

  // Notes on the sheet:
  //   Encoder 8 X 3
  //   _____________________________
  //   _____________________________
endmodule
