// Logisim project Even_or_OddCounter.circ as structural Verilog: 1 circuit, main circuit main
module main (
  input  in_1
);

  wire and_1_out, and_2_out, bcd_to_7_segment_decoder_1_p1, bcd_to_7_segment_decoder_1_p2,
       bcd_to_7_segment_decoder_1_p3, bcd_to_7_segment_decoder_1_p4, bcd_to_7_segment_decoder_1_p6,
       bcd_to_7_segment_decoder_1_p7, bcd_to_7_segment_decoder_1_p8, bcd_to_7_segment_decoder_2_p1,
       bcd_to_7_segment_decoder_2_p2, bcd_to_7_segment_decoder_2_p3, bcd_to_7_segment_decoder_2_p4,
       bcd_to_7_segment_decoder_2_p6, bcd_to_7_segment_decoder_2_p7, bcd_to_7_segment_decoder_2_p8, CLK_out,
       j_k_ff_2_qn, j_k_ff_4_qn, j_k_ff_6_qn, or_1_out, or_2_out, Reset_out;
  wire [3:0] bcd_to_7_segment_decoder_1_p5;
  wire [3:1] bcd_to_7_segment_decoder_2_p5;

  Button Reset (.out(Reset_out));
  Clock CLK (.out(CLK_out));
  J_K_Flip_Flop #(.trigger("falling")) j_k_ff_1 (
    .J(1'b1), .K(1'b1), .clk(bcd_to_7_segment_decoder_1_p5[2]), .Q(bcd_to_7_segment_decoder_1_p5[3]),
    .reset(or_1_out));  // open: Qn, preset
  or or_1 (or_1_out, Reset_out, and_1_out);
  and and_1 (and_1_out, bcd_to_7_segment_decoder_1_p5[3], j_k_ff_2_qn, bcd_to_7_segment_decoder_1_p5[1], j_k_ff_4_qn);
  // BCD_to_7_Segment_decoder bcd_to_7_segment_decoder_1: pin names not known; wires that end beside it: bcd_to_7_segment_decoder_1_p1, bcd_to_7_segment_decoder_1_p2, bcd_to_7_segment_decoder_1_p3, bcd_to_7_segment_decoder_1_p4, bcd_to_7_segment_decoder_1_p5, bcd_to_7_segment_decoder_1_p6, bcd_to_7_segment_decoder_1_p7, bcd_to_7_segment_decoder_1_p8
  J_K_Flip_Flop #(.trigger("falling")) j_k_ff_2 (
    .J(1'b1), .K(1'b1), .clk(bcd_to_7_segment_decoder_1_p5[1]), .Q(bcd_to_7_segment_decoder_1_p5[2]),
    .Qn(j_k_ff_2_qn), .reset(or_1_out));  // open: preset
  J_K_Flip_Flop #(.trigger("falling")) j_k_ff_3 (
    .J(1'b1), .K(1'b1), .clk(bcd_to_7_segment_decoder_1_p5[0]), .Q(bcd_to_7_segment_decoder_1_p5[1]),
    .reset(or_1_out));  // open: Qn, preset
  J_K_Flip_Flop j_k_ff_4 (
    .J(1'b1), .K(1'b1), .clk(or_2_out), .Q(bcd_to_7_segment_decoder_1_p5[0]), .Qn(j_k_ff_4_qn),
    .reset(or_1_out));  // open: preset
  _7_Segment_Display u_7_segment_display_1 (
    .g(bcd_to_7_segment_decoder_1_p1), .f(bcd_to_7_segment_decoder_1_p3), .a(bcd_to_7_segment_decoder_1_p6),
    .b(bcd_to_7_segment_decoder_1_p8), .e(bcd_to_7_segment_decoder_1_p2), .d(bcd_to_7_segment_decoder_1_p4),
    .c(bcd_to_7_segment_decoder_1_p7));  // open: dp
  _7_Segment_Display u_7_segment_display_2 (
    .g(bcd_to_7_segment_decoder_2_p1), .f(bcd_to_7_segment_decoder_2_p3), .a(bcd_to_7_segment_decoder_2_p6),
    .b(bcd_to_7_segment_decoder_2_p8), .e(bcd_to_7_segment_decoder_2_p2), .d(bcd_to_7_segment_decoder_2_p4),
    .c(bcd_to_7_segment_decoder_2_p7));  // open: dp
  J_K_Flip_Flop #(.trigger("falling")) j_k_ff_5 (
    .J(1'b1), .K(1'b1), .clk(bcd_to_7_segment_decoder_2_p5[2]), .Q(bcd_to_7_segment_decoder_2_p5[3]),
    .reset(or_2_out));  // open: Qn, preset
  or or_2 (or_2_out, Reset_out, and_2_out);
  and and_2 (and_2_out, bcd_to_7_segment_decoder_2_p5[3], j_k_ff_6_qn, bcd_to_7_segment_decoder_2_p5[1]);
  J_K_Flip_Flop #(.trigger("falling")) j_k_ff_6 (
    .J(1'b1), .K(1'b1), .clk(bcd_to_7_segment_decoder_2_p5[1]), .Q(bcd_to_7_segment_decoder_2_p5[2]),
    .Qn(j_k_ff_6_qn), .reset(or_2_out));  // open: preset
  // BCD_to_7_Segment_decoder bcd_to_7_segment_decoder_2: pin names not known; wires that end beside it: bcd_to_7_segment_decoder_2_p1, bcd_to_7_segment_decoder_2_p2, bcd_to_7_segment_decoder_2_p3, bcd_to_7_segment_decoder_2_p4, {bcd_to_7_segment_decoder_2_p5, in_1}, bcd_to_7_segment_decoder_2_p6, bcd_to_7_segment_decoder_2_p7, bcd_to_7_segment_decoder_2_p8
  J_K_Flip_Flop #(.trigger("falling")) j_k_ff_7 (
    .J(1'b1), .K(1'b1), .clk(CLK_out), .Q(bcd_to_7_segment_decoder_2_p5[1]), .reset(or_2_out));  // open: Qn, preset

  // Notes on the sheet:
  //   __________
  //   __________
  //   |
  //   |
  //   |
  //   |
  //   0 - Even
  //   |
  //   |
  //   |
  //   |
  //   1 - Odd
  //   |
  //   __________
  //   |
  //   __________
  //   Odd / Even
  //   |
  //   |
  //   |
  //   |
  //   |
  //   |
  //   |
  //   |
  //   |
  //   |
  //   Even / Odd Counter
  //   ~ ~ ~ ~ ~ ~ ~ ~ ~ ~ ~ ~ ~ ~ ~ ~ ~ ~ ~ ~ ~ ~ ~ ~ ~ ~ ~ ~ ~ ~
  //   ~ ~ ~ ~ ~ ~ ~ ~ ~ ~ ~ ~ ~ ~ ~ ~ ~ ~ ~ ~ ~ ~ ~ ~ ~ ~ ~ ~ ~ ~
endmodule
