// Logisim project Full_Subtractor.circ as structural Verilog: 1 circuit, main circuit main
module main (
  input  A,
  input  B,
  input  C,
  output Difference,
  output Borrow
);

  wire and_1_out, and_2_out, and_3_out, not_1_out, xnor_1_out, xor_1_out;

  not not_1 (not_1_out, A);
  xnor xnor_1 (xnor_1_out, B, C);
  xor xor_1 (xor_1_out, B, C);
  and and_1 (and_1_out, xnor_1_out, A);
  and and_2 (and_2_out, not_1_out, xor_1_out);
  and and_3 (and_3_out, C, B);
  or or_1 (Difference, and_1_out, and_2_out);
  or or_2 (Borrow, and_2_out, and_3_out);

  // Notes on the sheet:
  //   B'C'+BC
  //   B'C+BC'
  //   A(B'C'+BC)
  //   A'(B'C+BC')
  //   BC
  //   Full Subtractor
endmodule
