// Logisim project Half_Adder.circ as structural Verilog: 1 circuit, main circuit main
module main (
  input  A,
  input  B,
  output Sum,
  output Carry
);

  xor xor_1 (Sum, A, B);
  and and_1 (Carry, B, A);

  // Notes on the sheet:
  //   A'B+AB'
  //   AB
  //   Half Adder
endmodule
