// Logisim project Latches.circ as structural Verilog
module Gated_SRlatch (
  input  R,
  input  E,
  input  S,
  output Q,
  output Q_prime
);

  wire and_1_out, and_2_out;

  and and_1 (and_1_out, R, E);
  and and_2 (and_2_out, E, S);
  nor nor_1 (Q, and_1_out, Q_prime);
  nor nor_2 (Q_prime, Q, and_2_out);

  // Notes on the sheet:
  //   Gated SR Latch
endmodule

module SRflipflop (
  input  R,
  input  S,
  output Q,
  output Q_prime
);

  wire and_1_out, and_2_out, CLK_out;

  Clock CLK (.out(CLK_out));
  and and_1 (and_1_out, R, CLK_out);
  and and_2 (and_2_out, CLK_out, S);
  nor nor_1 (Q, and_1_out, Q_prime);
  nor nor_2 (Q_prime, Q, and_2_out);

  // Notes on the sheet:
  //   SR Flipflop
endmodule

module Dflipflop (
  input  D,
  output Q,
  output Q_prime
);

  wire and_1_out, and_2_out, CLK_out, not_1_out;

  not not_1 (not_1_out, D);
  Clock CLK (.out(CLK_out));
  and and_1 (and_1_out, not_1_out, CLK_out);
  and and_2 (and_2_out, CLK_out, D);
  nor nor_1 (Q, and_1_out, Q_prime);
  nor nor_2 (Q_prime, Q, and_2_out);

  // Notes on the sheet:
  //   D Flipflop
endmodule

module JKflipflop (
  input  K,
  input  J,
  output Q,
  output Q_prime
);

  wire and_1_out, and_2_out, CLK_out, undriven, undriven_2;

  Clock CLK (.out(CLK_out));
  and and_1 (and_1_out, undriven, K, CLK_out);
  and and_2 (and_2_out, CLK_out, J, undriven_2);
  nor nor_1 (Q, and_1_out, undriven_2);
  nor nor_2 (Q_prime, undriven, and_2_out);

  // Notes on the sheet:
  //   JK Flipflop
endmodule

module Dlatch (
  input  D,
  input  E,
  output Q,
  output Q_prime
);

  wire and_1_out, and_2_out, not_1_out;

  not not_1 (not_1_out, D);
  and and_1 (and_1_out, not_1_out, E);
  and and_2 (and_2_out, E, D);
  nor nor_1 (Q, and_1_out, Q_prime);
  nor nor_2 (Q_prime, and_2_out, Q);

  // Notes on the sheet:
  //   D Latch
endmodule
