// Logisim project Multiplexer 16x1.circ as structural Verilog: 2 circuits, main circuit main
module main (
  input  I0,
  input  I1,
  input  I2,
  input  I3,
  input  I4,
  input  I5,
  input  I6,
  input  I7,
  input  I8,
  input  I9,
  input  I10,
  input  I11,
  input  I12,
  input  I13,
  input  I14,
  input  I15,
  input  in_17,
  input  in_18,
  input  in_19,
  input  in_20,
  output Y
);

  wire and_1_out, and_2_out, and_3_out, and_4_out, and_5_out, and_6_out, and_7_out, and_8_out, and_9_out,
       and_10_out, and_11_out, and_12_out, and_13_out, and_14_out, and_15_out, and_16_out, not_1_out,
       not_2_out, not_3_out, not_4_out;

  not not_1 (not_1_out, in_17);
  not not_2 (not_2_out, in_18);
  not not_3 (not_3_out, in_19);
  not not_4 (not_4_out, in_20);
  and and_1 (and_1_out, I0, not_1_out, not_2_out, not_3_out, not_4_out);
  and and_2 (and_2_out, I1, not_1_out, not_2_out, not_3_out, in_20);
  and and_3 (and_3_out, I2, not_2_out, not_1_out, in_19, not_4_out);
  and and_4 (and_4_out, I3, not_1_out, not_2_out, in_19, in_20);
  and and_5 (and_5_out, I4, not_1_out, in_18, not_3_out, not_4_out);
  and and_6 (and_6_out, I5, not_1_out, in_18, not_3_out, in_20);
  and and_7 (and_7_out, I6, not_1_out, in_18, in_19, not_4_out);
  and and_8 (and_8_out, I7, not_1_out, in_18, in_19, in_20);
  and and_9 (and_9_out, I8, in_17, not_2_out, not_3_out, not_4_out);
  and and_10 (and_10_out, I9, in_17, not_2_out, not_3_out, in_20);
  and and_11 (and_11_out, I10, in_17, not_2_out, in_19, not_4_out);
  and and_12 (and_12_out, I11, in_17, not_2_out, in_19, in_20);
  and and_13 (and_13_out, I12, in_17, in_18, not_3_out, not_4_out);
  and and_14 (and_14_out, I13, in_17, not_3_out, in_18, in_20);
  and and_15 (and_15_out, I14, not_4_out, in_17, in_18, in_19);
  and and_16 (and_16_out, I15, in_17, in_19, in_18, in_20);
  or or_1 (Y, and_1_out, and_2_out, and_3_out, and_4_out, and_5_out, and_6_out, and_7_out, and_8_out, and_9_out, and_10_out, and_11_out, and_12_out, and_13_out, and_14_out, and_15_out, and_16_out);

  // Notes on the sheet:
  //   S3
  //   S2
  //   S1
  //   S0
  //   Multiplexer 16x1
  //   _________________
  //   _________________
endmodule

module Block_diagram (
  input  in_1,
  input  in_2,
  input  in_3,
  input  in_4,
  input  in_5,
  input  in_6,
  input  in_7,
  input  in_8,
  input  in_9,
  input  in_10,
  input  in_11,
  input  in_12,
  input  in_13,
  input  in_14,
  input  in_15,
  input  in_16,
  input  [3:0] in_17,
  output out_18
);

  Multiplexer #(.select(4)) multiplexer_1 (
    .in0(in_1), .in1(in_2), .in2(in_3), .in3(in_4), .in4(in_5), .in5(in_6), .in6(in_7), .in7(in_8),
    .in8(in_9), .in9(in_10), .in10(in_11), .in11(in_12), .in12(in_13), .in13(in_14), .in14(in_15),
    .in15(in_16), .out(out_18), .sel(in_17));
endmodule
