// Logisim project Multiplexer 4x1.circ as structural Verilog: 2 circuits, main circuit main
module main (
  input  I0,
  input  I1,
  input  I2,
  input  I3,
  input  S0,
  input  S1,
  output Y
);

  wire and_1_out, and_2_out, and_3_out, and_4_out, not_1_out, not_2_out;

  not not_1 (not_1_out, S0);
  not not_2 (not_2_out, S1);
  and and_1 (and_1_out, I0, not_1_out, not_2_out);
  and and_2 (and_2_out, I1, not_1_out, S1);
  and and_3 (and_3_out, I2, S0, not_2_out);
  and and_4 (and_4_out, S1, I3, S0);
  or or_1 (Y, and_1_out, and_2_out, and_3_out, and_4_out);

  // Notes on the sheet:
  //   Multiplexer 4x1
  //   _________________
  //   _________________
endmodule

module Block_diagram (
  input  in_1,
  input  in_2,
  input  in_3,
  input  in_4,
  input  [1:0] in_5,
  output out_6
);

  Multiplexer #(.select(2)) multiplexer_1 (.in0(in_1), .in1(in_2), .in2(in_3), .in3(in_4), .out(out_6), .sel(in_5));
endmodule
