// Logisim project Multiplexers 8x1.circ as structural Verilog: 2 circuits, main circuit main
module main (
  input  I0,
  input  I1,
  input  I2,
  input  I3,
  input  I4,
  input  I5,
  input  I6,
  input  I7,
  input  in_9,
  input  in_10,
  input  in_11,
  output Y
);

  wire and_1_out, and_2_out, and_3_out, and_4_out, and_5_out, and_6_out, and_7_out, and_8_out, not_1_out,
       not_2_out, not_3_out;

  not not_1 (not_1_out, in_9);
  not not_2 (not_2_out, in_10);
  not not_3 (not_3_out, in_11);
  and and_1 (and_1_out, I0, not_1_out, not_2_out, not_3_out);
  and and_2 (and_2_out, I1, not_1_out, not_2_out, in_11);
  and and_3 (and_3_out, I2, not_1_out, in_10, not_3_out);
  and and_4 (and_4_out, I3, not_1_out, in_10, in_11);
  and and_5 (and_5_out, I4, in_9, not_2_out, not_3_out);
  and and_6 (and_6_out, I5, in_9, not_2_out, in_11);
  and and_7 (and_7_out, I6, in_9, in_10, not_3_out);
  and and_8 (and_8_out, I7, in_9, in_10, in_11);
  or or_1 (Y, and_1_out, and_2_out, and_3_out, and_4_out, and_5_out, and_6_out, and_7_out, and_8_out);

  // Notes on the sheet:
  //   S2
  //   S1
  //   S0
  //   Multiplexer 8x1
  //   _________________
  //   _________________
endmodule

module Block_diagram (
  input  in_1,
  input  in_2,
  input  in_3,
  input  in_4,
  input  in_5,
  input  in_6,
  input  in_7,
  input  in_8,
  input  [2:0] in_9,
  output out_10
);

  Multiplexer #(.select(3)) multiplexer_1 (
    .in0(in_1), .in1(in_2), .in2(in_3), .in3(in_4), .in4(in_5), .in5(in_6), .in6(in_7), .in7(in_8),
    .out(out_10), .sel(in_9));
endmodule
