// Logisim project Priority Encoders.circ as structural Verilog
module PEncoder4x2 (
  input  Y3,
  input  Y2,
  input  Y1,
  input  Y0,
  output A,
  output B
);

  wire and_1_out, not_1_out;

  not not_1 (not_1_out, Y2);
  or or_1 (A, Y3, Y2);
  and and_1 (and_1_out, not_1_out, Y1);
  or or_2 (B, Y3, and_1_out);
endmodule

module PEncoder8x3 (
  input  Y7,
  input  Y6,
  input  Y5,
  input  Y4,
  input  Y3,
  input  Y2,
  input  Y1,
  input  Y0,
  output A,
  output B,
  output C
);

  wire and_1_out, and_2_out, and_3_out, and_4_out, not_1_out, not_2_out, not_3_out, not_4_out, or_2_out,
       or_3_out;

  not not_1 (not_1_out, Y6);
  not not_2 (not_2_out, Y5);
  not not_3 (not_3_out, Y4);
  not not_4 (not_4_out, Y2);
  or or_1 (A, Y4, Y5, Y6, Y7);
  or or_2 (or_2_out, Y2, Y3);
  and and_1 (and_1_out, not_3_out, not_4_out, Y1);
  and and_2 (and_2_out, not_3_out, Y3);
  and and_3 (and_3_out, not_2_out, not_3_out, or_2_out);
  or or_3 (or_3_out, and_1_out, and_2_out, Y5);
  or or_4 (B, and_3_out, Y6, Y7);
  and and_4 (and_4_out, not_1_out, or_3_out);
  or or_5 (C, and_4_out, Y7);
endmodule

module Block_diagram4x2 (
  input  in_1,
  input  in_2,
  input  in_3,
  input  in_4,
  output [1:0] out_5
);

  Priority_Encoder #(.select(2)) priority_encoder_1 (
    .in0(in_1), .in1(in_2), .in2(in_3), .in3(in_4), .out(out_5));  // open: gs, en_out, en_in
endmodule

module Block_diagram8x3 (
  input  in_1,
  input  in_2,
  input  in_3,
  input  in_4,
  input  in_5,
  input  in_6,
  input  in_7,
  input  in_8,
  output [2:0] out_9
);

  Priority_Encoder priority_encoder_1 (
    .in0(in_1), .in1(in_2), .in2(in_3), .in3(in_4), .in4(in_5), .in5(in_6), .in6(in_7), .in7(in_8),
    .out(out_9));  // open: en_in, gs, en_out
endmodule
