// Logisim project S20210020303 ( Q1 ).circ as structural Verilog: 4 circuits, main circuit main
module main (
  input  [3:0] Input_A,
  input  [3:0] LSB,
  input  [3:0] Input_B,
  input  [3:0] LSB_2
);

  wire adder_1_cout, adder_2_cout, bcd_to_7_segment_decoder_1_p1, bcd_to_7_segment_decoder_1_p2,
       bcd_to_7_segment_decoder_1_p3, bcd_to_7_segment_decoder_1_p4, bcd_to_7_segment_decoder_1_p6,
       bcd_to_7_segment_decoder_1_p7, bcd_to_7_segment_decoder_2_p1, bcd_to_7_segment_decoder_2_p2,
       bcd_to_7_segment_decoder_2_p3, bcd_to_7_segment_decoder_2_p4, bcd_to_7_segment_decoder_2_p6,
       bcd_to_7_segment_decoder_2_p7, bcd_to_7_segment_decoder_3_p1, bcd_to_7_segment_decoder_3_p2,
       bcd_to_7_segment_decoder_3_p3, bcd_to_7_segment_decoder_3_p4, bcd_to_7_segment_decoder_3_p5,
       bcd_to_7_segment_decoder_3_p7, bcd_to_7_segment_decoder_3_p8, bcd_to_7_segment_decoder_3_p9,
       bcd_to_7_segment_decoder_4_p1, bcd_to_7_segment_decoder_4_p2, bcd_to_7_segment_decoder_4_p3,
       bcd_to_7_segment_decoder_4_p4, bcd_to_7_segment_decoder_4_p5, bcd_to_7_segment_decoder_4_p7,
       bcd_to_7_segment_decoder_4_p8, bcd_to_7_segment_decoder_4_p9, bcd_to_7segment_1_a,
       bcd_to_7segment_1_c, bcd_to_7segment_1_d, bcd_to_7segment_1_e, bcd_to_7segment_1_f,
       bcd_to_7segment_1_g, bcd_to_7segment_1_out_6, bcd_to_7segment_2_a, bcd_to_7segment_2_c,
       bcd_to_7segment_2_d, bcd_to_7segment_2_e, bcd_to_7segment_2_f, bcd_to_7segment_2_g,
       bcd_to_7segment_2_out_6, binary_to_bcd_1_a, binary_to_bcd_1_b, binary_to_bcd_1_cout,
       binary_to_bcd_1_out_9, binary_to_bcd_1_out_10, binary_to_bcd_2_a, binary_to_bcd_2_b,
       binary_to_bcd_2_cout, binary_to_bcd_2_out_9, binary_to_bcd_2_out_10, hundreth_place_1_a,
       hundreth_place_1_b, hundreth_place_1_c, hundreth_place_1_d, hundreth_place_1_e, hundreth_place_1_f,
       hundreth_place_1_g;
  wire [3:0] adder_1_out, adder_2_out;

  // BCD_to_7_Segment_decoder bcd_to_7_segment_decoder_1: pin names not known; wires that end beside it: bcd_to_7_segment_decoder_1_p1, bcd_to_7_segment_decoder_1_p2, bcd_to_7_segment_decoder_1_p3, bcd_to_7_segment_decoder_1_p4, Input_A, bcd_to_7_segment_decoder_1_p6, bcd_to_7_segment_decoder_1_p7
  // BCD_to_7_Segment_decoder bcd_to_7_segment_decoder_2: pin names not known; wires that end beside it: bcd_to_7_segment_decoder_2_p1, bcd_to_7_segment_decoder_2_p2, bcd_to_7_segment_decoder_2_p3, bcd_to_7_segment_decoder_2_p4, Input_B, bcd_to_7_segment_decoder_2_p6, bcd_to_7_segment_decoder_2_p7
  // BCD_to_7_Segment_decoder bcd_to_7_segment_decoder_3: pin names not known; wires that end beside it: bcd_to_7_segment_decoder_3_p1, bcd_to_7_segment_decoder_3_p2, bcd_to_7_segment_decoder_3_p3, bcd_to_7_segment_decoder_3_p4, bcd_to_7_segment_decoder_3_p5, LSB, bcd_to_7_segment_decoder_3_p7, bcd_to_7_segment_decoder_3_p8, bcd_to_7_segment_decoder_3_p9
  // BCD_to_7_Segment_decoder bcd_to_7_segment_decoder_4: pin names not known; wires that end beside it: bcd_to_7_segment_decoder_4_p1, bcd_to_7_segment_decoder_4_p2, bcd_to_7_segment_decoder_4_p3, bcd_to_7_segment_decoder_4_p4, bcd_to_7_segment_decoder_4_p5, LSB_2, bcd_to_7_segment_decoder_4_p7, bcd_to_7_segment_decoder_4_p8, bcd_to_7_segment_decoder_4_p9
  _7_Segment_Display u_7_segment_display_1 (
    .g(bcd_to_7_segment_decoder_1_p1), .f(bcd_to_7_segment_decoder_1_p3), .a(bcd_to_7_segment_decoder_1_p6),
    .b(bcd_to_7_segment_decoder_3_p1), .e(bcd_to_7_segment_decoder_1_p2), .d(bcd_to_7_segment_decoder_1_p4),
    .c(bcd_to_7_segment_decoder_1_p7));  // open: dp
  _7_Segment_Display u_7_segment_display_2 (
    .g(bcd_to_7_segment_decoder_2_p1), .f(bcd_to_7_segment_decoder_2_p3), .a(bcd_to_7_segment_decoder_2_p6),
    .b(bcd_to_7_segment_decoder_4_p1), .e(bcd_to_7_segment_decoder_2_p2), .d(bcd_to_7_segment_decoder_2_p4),
    .c(bcd_to_7_segment_decoder_2_p7));  // open: dp
  _7_Segment_Display u_7_segment_display_3 (
    .g(bcd_to_7_segment_decoder_3_p2), .f(bcd_to_7_segment_decoder_3_p4), .a(bcd_to_7_segment_decoder_3_p7),
    .b(bcd_to_7_segment_decoder_3_p9), .e(bcd_to_7_segment_decoder_3_p3), .d(bcd_to_7_segment_decoder_3_p5),
    .c(bcd_to_7_segment_decoder_3_p8));  // open: dp
  _7_Segment_Display u_7_segment_display_4 (
    .g(bcd_to_7_segment_decoder_4_p2), .f(bcd_to_7_segment_decoder_4_p4), .a(bcd_to_7_segment_decoder_4_p7),
    .b(bcd_to_7_segment_decoder_4_p9), .e(bcd_to_7_segment_decoder_4_p3), .d(bcd_to_7_segment_decoder_4_p5),
    .c(bcd_to_7_segment_decoder_4_p8));  // open: dp
  Adder #(.width(4)) adder_1 (.a(LSB), .b(LSB_2), .out(adder_1_out), .cout(adder_1_cout));  // open: cin
  Adder #(.width(4)) adder_2 (
    .a(Input_A), .b(Input_B), .out(adder_2_out), .cin(binary_to_bcd_1_cout), .cout(adder_2_cout));
  Binary_to_BCD binary_to_bcd_1 (
    .Cin(adder_1_cout), .in_2(adder_1_out[3]), .in_3(adder_1_out[2]), .C(adder_1_out[1]), .D(adder_1_out[0]),
    .Cout(binary_to_bcd_1_cout), .a(binary_to_bcd_1_a), .b(binary_to_bcd_1_b), .out_9(binary_to_bcd_1_out_9),
    .out_10(binary_to_bcd_1_out_10));
  Binary_to_BCD binary_to_bcd_2 (
    .Cin(adder_2_cout), .in_2(adder_2_out[3]), .in_3(adder_2_out[2]), .C(adder_2_out[1]), .D(adder_2_out[0]),
    .Cout(binary_to_bcd_2_cout), .a(binary_to_bcd_2_a), .b(binary_to_bcd_2_b), .out_9(binary_to_bcd_2_out_9),
    .out_10(binary_to_bcd_2_out_10));
  BCD_to_7segment bcd_to_7segment_1 (
    .in_1(binary_to_bcd_1_a), .B(binary_to_bcd_1_b), .in_3(binary_to_bcd_1_out_9),
    .in_4(binary_to_bcd_1_out_10), .a(bcd_to_7segment_1_a), .out_6(bcd_to_7segment_1_out_6),
    .c(bcd_to_7segment_1_c), .d(bcd_to_7segment_1_d), .e(bcd_to_7segment_1_e), .f(bcd_to_7segment_1_f),
    .g(bcd_to_7segment_1_g));
  BCD_to_7segment bcd_to_7segment_2 (
    .in_1(binary_to_bcd_2_a), .B(binary_to_bcd_2_b), .in_3(binary_to_bcd_2_out_9),
    .in_4(binary_to_bcd_2_out_10), .a(bcd_to_7segment_2_a), .out_6(bcd_to_7segment_2_out_6),
    .c(bcd_to_7segment_2_c), .d(bcd_to_7segment_2_d), .e(bcd_to_7segment_2_e), .f(bcd_to_7segment_2_f),
    .g(bcd_to_7segment_2_g));
  Hundreth_place hundreth_place_1 (
    .Cin(binary_to_bcd_2_cout), .a(hundreth_place_1_a), .b(hundreth_place_1_b), .c(hundreth_place_1_c),
    .d(hundreth_place_1_d), .e(hundreth_place_1_e), .f(hundreth_place_1_f), .g(hundreth_place_1_g));
  _7_Segment_Display u_7_segment_display_5 (
    .g(hundreth_place_1_g), .f(hundreth_place_1_f), .a(hundreth_place_1_a), .b(hundreth_place_1_b),
    .e(hundreth_place_1_e), .d(hundreth_place_1_d), .c(hundreth_place_1_c));  // open: dp
  _7_Segment_Display u_7_segment_display_6 (
    .g(bcd_to_7segment_2_g), .f(bcd_to_7segment_2_f), .a(bcd_to_7segment_2_a), .b(bcd_to_7segment_2_out_6),
    .e(bcd_to_7segment_2_e), .d(bcd_to_7segment_2_d), .c(bcd_to_7segment_2_c));  // open: dp
  _7_Segment_Display u_7_segment_display_7 (
    .g(bcd_to_7segment_1_g), .f(bcd_to_7segment_1_f), .a(bcd_to_7segment_1_a), .b(bcd_to_7segment_1_out_6),
    .e(bcd_to_7segment_1_e), .d(bcd_to_7segment_1_d), .c(bcd_to_7segment_1_c));  // open: dp

  // Notes on the sheet:
  //   MSB
  //   MSB
  //   Q1)           Addition of two decimal numbers
endmodule

module Binary_to_BCD (
  input  Cin,
  input  in_2,
  input  in_3,
  input  C,
  input  D,
  output Cout,
  output a,
  output b,
  output out_9,
  output out_10
);

  wire and_1_out, and_2_out, and_3_out, and_4_out, and_5_out, and_6_out, and_7_out, and_8_out, and_9_out,
       and_10_out, not_1_out, not_2_out, not_3_out, not_4_out;

  not not_1 (not_1_out, Cin);
  not not_2 (not_2_out, in_2);
  not not_3 (not_3_out, in_3);
  not not_4 (not_4_out, C);
  and and_1 (and_1_out, in_2, C);
  and and_2 (and_2_out, in_2, in_3);
  and and_3 (and_3_out, in_2, not_3_out, not_4_out);
  and and_4 (and_4_out, Cin, C);
  and and_5 (and_5_out, not_2_out, in_3);
  and and_6 (and_6_out, in_3, C);
  and and_7 (and_7_out, Cin, not_4_out);
  and and_8 (and_8_out, not_1_out, not_2_out, C);
  and and_9 (and_9_out, in_2, in_3, not_4_out);
  and and_10 (and_10_out, Cin, not_4_out);
  or or_1 (Cout, and_1_out, and_2_out, Cin);
  or or_2 (a, and_3_out, and_4_out);
  or or_3 (b, and_5_out, and_6_out, and_7_out);
  or or_4 (out_9, and_8_out, and_9_out, and_10_out);

  assign out_10 = D;
endmodule

module BCD_to_7segment (
  input  in_1,
  input  B,
  input  in_3,
  input  in_4,
  output a,
  output out_6,
  output c,
  output d,
  output e,
  output f,
  output g
);

  wire and_1_out, and_2_out, and_3_out, and_4_out, and_5_out, and_6_out, and_7_out, and_8_out, and_9_out,
       and_10_out, and_11_out, and_12_out, and_13_out, and_14_out, and_15_out, and_16_out, not_1_out,
       not_2_out, not_3_out;

  not not_1 (not_1_out, B);
  not not_2 (not_2_out, in_3);
  not not_3 (not_3_out, in_4);
  and and_1 (and_1_out, not_1_out, not_3_out);
  and and_2 (and_2_out, B, in_4);
  and and_3 (and_3_out, not_2_out, not_3_out);
  and and_4 (and_4_out, in_3, in_4);
  or or_1 (c, not_2_out, in_4, B);
  and and_5 (and_5_out, not_1_out, not_3_out);
  and and_6 (and_6_out, not_1_out, in_3);
  and and_7 (and_7_out, in_3, not_3_out);
  and and_8 (and_8_out, B, not_2_out, in_4);
  and and_9 (and_9_out, not_1_out, not_3_out);
  and and_10 (and_10_out, in_3, not_3_out);
  and and_11 (and_11_out, not_2_out, not_3_out);
  and and_12 (and_12_out, B, not_2_out);
  and and_13 (and_13_out, B, not_3_out);
  and and_14 (and_14_out, not_1_out, in_3);
  and and_15 (and_15_out, B, not_2_out);
  and and_16 (and_16_out, B, not_3_out);
  or or_2 (a, and_1_out, in_3, and_2_out, in_1);
  or or_3 (out_6, not_1_out, and_3_out, and_4_out);
  or or_4 (d, and_5_out, and_6_out, and_7_out, and_8_out, in_1);
  or or_5 (e, and_9_out, and_10_out);
  or or_6 (f, and_11_out, and_12_out, and_13_out, in_1);
  or or_7 (g, and_14_out, and_15_out, and_16_out, in_1);
endmodule

module Hundreth_place (
  input  Cin,
  output a,
  output b,
  output c,
  output d,
  output e,
  output f,
  output g
);

  not not_1 (a, Cin);

  assign b = 1'b1;
  assign c = 1'b1;
  assign d = a;
  assign e = a;
  assign f = a;
  assign g = 1'b0;
endmodule
