// Logisim project S20210020303 ( Q2-Q5 ).circ as structural Verilog
module One_bit_fulladder (
  input  Input_A,
  input  Input_B,
  input  Cin,
  output Sum,
  output Cout
);

  wire and_1_out, and_2_out, xor_1_out;

  xor xor_1 (xor_1_out, Input_A, Input_B);
  and and_1 (and_1_out, Input_A, Input_B);
  xor xor_2 (Sum, xor_1_out, Cin);
  and and_2 (and_2_out, Cin, xor_1_out);
  or or_1 (Cout, and_2_out, and_1_out);

  // Notes on the sheet:
  //   1 bit full adder
endmodule

module Four_bit_addition_of_2_numbers_using_fulladders (
  input  [3:0] Input_A,
  input  [3:0] Input_B,
  output [4:0] Sum
);

  wire one_bit_fulladder_1_cout, one_bit_fulladder_2_cout, one_bit_fulladder_3_cout;

  One_bit_fulladder one_bit_fulladder_1 (
    .Input_A(Input_A[0]), .Input_B(Input_B[0]), .Cin(1'b0), .Sum(Sum[0]), .Cout(one_bit_fulladder_1_cout));
  One_bit_fulladder one_bit_fulladder_2 (
    .Input_A(Input_A[1]), .Input_B(Input_B[1]), .Cin(one_bit_fulladder_1_cout), .Sum(Sum[1]),
    .Cout(one_bit_fulladder_2_cout));
  One_bit_fulladder one_bit_fulladder_3 (
    .Input_A(Input_A[2]), .Input_B(Input_B[2]), .Cin(one_bit_fulladder_2_cout), .Sum(Sum[2]),
    .Cout(one_bit_fulladder_3_cout));
  One_bit_fulladder one_bit_fulladder_4 (
    .Input_A(Input_A[3]), .Input_B(Input_B[3]), .Cin(one_bit_fulladder_3_cout), .Sum(Sum[3]), .Cout(Sum[4]));

  // Notes on the sheet:
  //   i)
  //   Q-2:
  //   4 Bit Full Adder
  //   Using 1bit Full Adders
endmodule

module One_bit_fulladder_with_Decoders (
  input  EN,
  input  A,
  input  B,
  input  Cin,
  output Sum,
  output Cout
);

  wire decoder_1_out1, decoder_1_out2, decoder_1_out3, decoder_1_out4, decoder_1_out5, decoder_1_out6,
       decoder_1_out7;

  Decoder #(.select(3)) decoder_1 (
    .out1(decoder_1_out1), .out2(decoder_1_out2), .out3(decoder_1_out3), .out4(decoder_1_out4),
    .out5(decoder_1_out5), .out6(decoder_1_out6), .out7(decoder_1_out7), .sel({Cin, B, A}), .en(EN));  // open: out0
  or or_1 (Sum, decoder_1_out1, decoder_1_out2, decoder_1_out4, decoder_1_out7);
  or or_2 (Cout, decoder_1_out3, decoder_1_out5, decoder_1_out6, decoder_1_out7);

  // Notes on the sheet:
  //   1 bit addition Using Decoders
endmodule

module Four_bit_addition_of_2_numbers_using_Decoders (
  input  [3:0] Input_A,
  input  [3:0] Input_B,
  output [4:0] Sum
);

  wire one_bit_fulladder_with_decoders_1_cout, one_bit_fulladder_with_decoders_2_cout,
       one_bit_fulladder_with_decoders_3_cout;

  One_bit_fulladder_with_Decoders one_bit_fulladder_with_decoders_1 (
    .EN(1'b1), .A(Input_A[0]), .B(Input_B[0]), .Cin(1'b0), .Sum(Sum[0]),
    .Cout(one_bit_fulladder_with_decoders_1_cout));
  One_bit_fulladder_with_Decoders one_bit_fulladder_with_decoders_2 (
    .EN(1'b1), .A(Input_A[1]), .B(Input_B[1]), .Cin(one_bit_fulladder_with_decoders_1_cout), .Sum(Sum[1]),
    .Cout(one_bit_fulladder_with_decoders_2_cout));
  One_bit_fulladder_with_Decoders one_bit_fulladder_with_decoders_3 (
    .EN(1'b1), .A(Input_A[2]), .B(Input_B[2]), .Cin(one_bit_fulladder_with_decoders_2_cout), .Sum(Sum[2]),
    .Cout(one_bit_fulladder_with_decoders_3_cout));
  One_bit_fulladder_with_Decoders one_bit_fulladder_with_decoders_4 (
    .EN(1'b1), .A(Input_A[3]), .B(Input_B[3]), .Cin(one_bit_fulladder_with_decoders_3_cout), .Sum(Sum[3]),
    .Cout(Sum[4]));

  // Notes on the sheet:
  //   ii)
  //   Q-2:
  //   4 Bit Full Adder
  //   Using Decoders
endmodule

module Addition_and_Subtraction_of_1_bit_numbers (
  input  Input_A,
  input  Input_B,
  input  Enabler_for_Subtraction,
  output out_4,
  output SUM,
  output Borrow,
  output Difference
);

  wire and_1_out, and_2_out, and_5_out, not_1_out, not_2_out, not_3_out, not_4_out, not_5_out, not_6_out,
       not_7_out;

  not not_1 (not_1_out, Input_A);
  not not_2 (not_2_out, Enabler_for_Subtraction);
  not not_3 (not_3_out, Input_B);
  not not_4 (not_4_out, Enabler_for_Subtraction);
  not not_5 (not_5_out, Enabler_for_Subtraction);
  not not_6 (not_6_out, Input_A);
  not not_7 (not_7_out, Input_B);
  and and_1 (and_1_out, not_1_out, Input_B, not_2_out);
  and and_2 (and_2_out, Input_A, not_3_out, not_4_out);
  and and_3 (out_4, Input_A, Input_B, not_5_out);
  and and_4 (Borrow, not_6_out, Input_B, Enabler_for_Subtraction);
  and and_5 (and_5_out, Input_A, not_7_out, Enabler_for_Subtraction);
  or or_1 (SUM, and_1_out, and_2_out);
  or or_2 (Difference, Borrow, and_5_out);
endmodule

module Four_bit_comparator (
  input  [3:0] in_1,
  input  [3:0] in_2,
  input  Enable,
  output out_4,
  output out_5,
  output out_6
);

  wire and_1_out, and_2_out, and_3_out, and_4_out, and_5_out, and_6_out, and_7_out, and_8_out, xnor_1_out,
       xnor_2_out, xnor_3_out, xnor_4_out;

  xnor xnor_1 (xnor_1_out, in_1[0], in_2[0]);
  xnor xnor_2 (xnor_2_out, in_1[1], in_2[1]);
  xnor xnor_3 (xnor_3_out, in_1[2], in_2[2]);
  xnor xnor_4 (xnor_4_out, in_1[3], in_2[3]);
  and and_1 (and_1_out, in_1[3], Enable, ~in_2[3]);  // AND_Gate
  and and_2 (and_2_out, in_1[2], xnor_4_out, Enable, ~in_2[2]);  // AND_Gate
  and and_3 (and_3_out, in_1[1], xnor_3_out, Enable, xnor_4_out, ~in_2[1]);  // AND_Gate
  and and_4 (and_4_out, in_1[0], xnor_2_out, xnor_3_out, xnor_4_out, Enable, ~in_2[0]);  // AND_Gate
  and and_5 (and_5_out, ~in_1[3], Enable, in_2[3]);  // AND_Gate
  and and_6 (and_6_out, ~in_1[2], xnor_4_out, Enable, in_2[2]);  // AND_Gate
  and and_7 (and_7_out, ~in_1[1], xnor_3_out, Enable, xnor_4_out, in_2[1]);  // AND_Gate
  and and_8 (and_8_out, ~in_1[0], xnor_2_out, Enable, xnor_3_out, xnor_4_out, in_2[0]);  // AND_Gate
  and and_9 (out_4, xnor_1_out, xnor_2_out, Enable, xnor_3_out, xnor_4_out);
  or or_1 (out_5, and_1_out, and_2_out, and_3_out, and_4_out);
  or or_2 (out_6, and_5_out, and_6_out, and_7_out, and_8_out);
  LED led_1 (.in(out_4));
  LED led_2 (.in(out_5));
  LED led_3 (.in(out_6));

  // Notes on the sheet:
  //   Input A
  //   Input B
  //   4 Bit comaparator
  //   A Equal to B
  //   A is Greater
  //   B is Greater
endmodule

module Eight_bit_comparator_using_4bit_and_logicgates (
  input  [7:0] in_1,
  input  [7:0] in_2,
  output out_3,
  output out_4,
  output out_5
);

  wire four_bit_comparator_1_out_4, four_bit_comparator_1_out_5, four_bit_comparator_1_out_6,
       four_bit_comparator_2_out_5, four_bit_comparator_2_out_6;

  Four_bit_comparator four_bit_comparator_1 (
    .in_1(in_1[7:4]), .in_2(in_2[7:4]), .Enable(1'b1), .out_4(four_bit_comparator_1_out_4),
    .out_5(four_bit_comparator_1_out_5), .out_6(four_bit_comparator_1_out_6));
  Four_bit_comparator four_bit_comparator_2 (
    .in_1(in_1[3:0]), .in_2(in_2[3:0]), .Enable(four_bit_comparator_1_out_4), .out_4(out_4),
    .out_5(four_bit_comparator_2_out_5), .out_6(four_bit_comparator_2_out_6));
  or or_1 (out_3, four_bit_comparator_1_out_5, four_bit_comparator_2_out_5);
  or or_2 (out_5, four_bit_comparator_1_out_6, four_bit_comparator_2_out_6);
  LED led_1 (.in(out_3));
  LED led_2 (.in(out_4));
  LED led_3 (.in(out_5));

  // Notes on the sheet:
  //   Input A
  //   Input B
  //   Q-4:
  //   A
  //   B
  //   A
  //   B
  //   8 Bit Comparator
  //   Using 4 bit comaparator
  //   A = B
  //   A > B
  //   B > A
  //   A = B
  //   A > B
  //   B > A
  //   B is Greater
  //   A is Greater
  //   A Equal to B
endmodule

module Decoder_5x32_using_3x8_decoder (
  input  [4:0] Innput_A,
  output D0,
  output D1,
  output D2,
  output D3,
  output D4,
  output D5,
  output D6,
  output D7,
  output D8,
  output D9,
  output D10,
  output D11,
  output D12,
  output D13,
  output D14,
  output D15,
  output D16,
  output D17,
  output D18,
  output D19,
  output D20,
  output D21,
  output D22,
  output D23,
  output D24,
  output D25,
  output D26,
  output D27,
  output D28,
  output D29,
  output D30,
  output D31
);

  wire decoder_1_out0, decoder_1_out1, decoder_1_out2, decoder_1_out3;

  Decoder #(.select(3)) decoder_1 (
    .out0(decoder_1_out0), .out1(decoder_1_out1), .out2(decoder_1_out2), .out3(decoder_1_out3),
    .sel({1'b0, Innput_A[4:3]}), .en(1'b1));  // open: out4, out5, out6, out7
  Decoder #(.select(3)) decoder_2 (
    .out0(D0), .out1(D1), .out2(D2), .out3(D3), .out4(D4), .out5(D5), .out6(D6), .out7(D7),
    .sel(Innput_A[2:0]), .en(decoder_1_out0));
  Decoder #(.select(3)) decoder_3 (
    .out0(D8), .out1(D9), .out2(D10), .out3(D11), .out4(D12), .out5(D13), .out6(D14), .out7(D15),
    .sel(Innput_A[2:0]), .en(decoder_1_out1));
  Decoder #(.select(3)) decoder_4 (
    .out0(D16), .out1(D17), .out2(D18), .out3(D19), .out4(D20), .out5(D21), .out6(D22), .out7(D23),
    .sel(Innput_A[2:0]), .en(decoder_1_out2));
  Decoder #(.select(3)) decoder_5 (
    .out0(D24), .out1(D25), .out2(D26), .out3(D27), .out4(D28), .out5(D29), .out6(D30), .out7(D31),
    .sel(Innput_A[2:0]), .en(decoder_1_out3));

  // Notes on the sheet:
  //   Q-5:
  //   5 x 32 Decoder
  //   Using 3 x 8 decoder
endmodule
