// Logisim project S20210020303 function using MUX.circ as structural Verilog: 2 circuits, main circuit Using_MUX
module Using_MUX (
  input  [3:0] A3_A2_A1_A0,
  output Y
);

  wire multiplexer_1_out, multiplexer_2_out, not_1_out, not_2_out;

  not not_1 (not_1_out, 1'b0);
  not not_2 (not_2_out, A3_A2_A1_A0[3]);
  Multiplexer #(.enable("true"), .select(3)) multiplexer_1 (
    .in0(1'b0), .in1(not_1_out), .in2(not_1_out), .in3(1'b0), .in4(1'b0), .in5(not_1_out), .in6(not_1_out),
    .in7(not_1_out), .out(multiplexer_1_out), .sel(A3_A2_A1_A0[2:0]), .en(not_2_out));
  Multiplexer #(.enable("true"), .select(3)) multiplexer_2 (
    .in0(not_1_out), .in1(1'b0), .in2(not_1_out), .in3(1'b0), .in4(not_1_out), .in5(not_1_out), .in6(1'b0),
    .in7(not_1_out), .out(multiplexer_2_out), .sel(A3_A2_A1_A0[2:0]), .en(A3_A2_A1_A0[3]));
  or or_1 (Y, multiplexer_1_out, multiplexer_2_out);

  // Notes on the sheet:
  //   Using MUX
endmodule

module Using_logicgates (
  input  [3:0] A3_A2_A1_A0,
  output Y
);

  wire and_1_out, and_2_out, and_3_out, and_4_out, and_5_out, not_1_out, not_2_out, not_3_out, not_4_out;

  not not_1 (not_1_out, A3_A2_A1_A0[3]);
  not not_2 (not_2_out, A3_A2_A1_A0[2]);
  not not_3 (not_3_out, A3_A2_A1_A0[1]);
  not not_4 (not_4_out, A3_A2_A1_A0[0]);
  and and_1 (and_1_out, A3_A2_A1_A0[2], A3_A2_A1_A0[0]);
  and and_2 (and_2_out, not_1_out, not_3_out, A3_A2_A1_A0[0]);
  and and_3 (and_3_out, not_1_out, A3_A2_A1_A0[1], not_4_out);
  and and_4 (and_4_out, A3_A2_A1_A0[3], not_2_out, not_4_out);
  and and_5 (and_5_out, A3_A2_A1_A0[3], not_3_out, not_4_out);
  or or_1 (Y, and_1_out, and_2_out, and_3_out, and_4_out, and_5_out);

  // Notes on the sheet:
  //   Using Logic gates
endmodule
