// Logisim project Serial_Multiplier.circ as structural Verilog: 2 circuits, main circuit Multiplier_4_bit
module Control_Unit (
  input  LSB,
  input  Count,
  input  Start,
  input  CLK,
  input  Reset,
  output Shift_EN,
  output Count_EN,
  output Add_EN,
  output MUX_EN,
  output Q_Load,
  output A_load
);

  wire A_FF_q, A_FF_qn, and_1_out, and_2_out, and_3_out, and_4_out, B_FF_q, B_FF_qn, not_1_out, or_1_out,
       or_2_out;

  not not_1 (not_1_out, Count);
  and and_1 (and_1_out, A_FF_qn, B_FF_q, not_1_out);
  and and_2 (and_2_out, A_FF_q, B_FF_qn, Count);
  and and_3 (and_3_out, B_FF_qn, Start, not_1_out);
  and and_4 (and_4_out, A_FF_q, B_FF_qn);
  or or_1 (or_1_out, and_1_out, and_2_out);
  or or_2 (or_2_out, and_3_out, and_4_out);
  D_Flip_Flop A_FF (.D(or_1_out), .clk(CLK), .Q(A_FF_q), .Qn(A_FF_qn), .reset(Reset));  // open: preset
  D_Flip_Flop B_FF (.D(or_2_out), .clk(CLK), .Q(B_FF_q), .Qn(B_FF_qn), .reset(Reset));  // open: preset
  and and_5 (A_load, A_FF_qn, B_FF_q, not_1_out, LSB);
  and and_6 (Q_Load, A_FF_qn, B_FF_qn, Start, not_1_out);
  and and_7 (Count_EN, B_FF_qn, A_FF_q);

  assign Add_EN = A_load;
  assign MUX_EN = A_load;
  assign Shift_EN = Count_EN;
endmodule

module Multiplier_4_bit (
  input  [3:0] O,
  input  Reset,
  input  Start,
  input  [3:0] Compare_value,
  input  [3:0] Multiplicand_M,
  input  [3:0] Multiplier_Q,
  output out_7,
  output [3:0] out_8,
  output [7:0] Answer
);

  wire A_p1, C_p5, Clk_out, comparator_1_eq, Control_Block_a_load, Control_Block_add_en,
       Control_Block_q_load, Control_Block_shift_en, not_1_out;
  wire [3:0] adder_1_out, multiplexer_1_out;

  Clock Clk (.out(Clk_out));
  Counter #(.max('hf), .width(4)) counter_1 (
    .clr(Reset), .up(Start), .count(not_1_out), .clk(Clk_out), .carry(out_7), .Q(out_8));  // open: load, D
  not not_1 (not_1_out, comparator_1_eq);
  LED led_1 (.in(comparator_1_eq));
  Comparator #(.width(4)) comparator_1 (.a(out_8), .b(Compare_value), .eq(comparator_1_eq));  // open: gt, lt
  Control_Unit Control_Block (
    .LSB(Answer[0]), .Count(comparator_1_eq), .Start(Start), .CLK(Clk_out), .Reset(Reset),
    .Shift_EN(Control_Block_shift_en), .Count_EN(Control_Block_shift_en), .Add_EN(Control_Block_add_en),
    .MUX_EN(Control_Block_add_en), .Q_Load(Control_Block_q_load), .A_load(Control_Block_a_load));
  Multiplexer #(.width(4)) multiplexer_1 (
    .in0(O), .in1(Multiplicand_M), .out(multiplexer_1_out), .sel(Control_Block_add_en));
  // Shift_Register #(.length(1)) C: pin names not known; wires that end beside it: Reset, Control_Block_a_load, Control_Block_shift_en, Clk_out, C_p5, C_p5
  Adder #(.width(4)) adder_1 (.a(multiplexer_1_out), .b(Answer[7:4]), .out(adder_1_out), .cout(C_p5));  // open: cin
  // Shift_Register #(.length(4)) A: pin names not known; wires that end beside it: A_p1, Reset, Control_Block_a_load, Control_Block_shift_en, Clk_out, A_p1, adder_1_out[3], adder_1_out[2], adder_1_out[1], adder_1_out[0]
  // Shift_Register #(.length(4)) Q: pin names not known; wires that end beside it: Answer[7], Answer[6], Answer[5], Answer[4], Reset, Control_Block_q_load, Control_Block_shift_en, Clk_out, Answer[4], Multiplier_Q[3], Multiplier_Q[2], Multiplier_Q[1], Multiplier_Q[0], Answer[3], Answer[2], Answer[1], Answer[0]

  // Notes on the sheet:
  //   Clock Cycles required are 9. Therefore, 9 is the Compare value
  //   4 Bit Serial Multiplier (Add & Shift Method) 
endmodule
