// Logisim project S20210020303_Assign1_Q1.circ as structural Verilog: 1 circuit, main circuit Without_feedback
module Without_feedback (
  input  Reset,
  input  Load,
  input  A_Shift,
  input  [3:0] A_Load,
  input  Sel,
  input  B_shift,
  input  [3:0] B_Load,
  output [3:0] Out_in_RegC
);

  wire Clk_out, multiplexer_1_out, not_1_out, Reg_B_p12, Reg_B_p13;

  Clock Clk (.out(Clk_out));
  not not_1 (not_1_out, Load);
  // Shift_Register #(.length(4)) Reg_A: pin names not known; wires that end beside it: Reset, Load, not_1_out, Clk_out, A_Shift, A_Load[3], A_Load[2]
  // Shift_Register #(.length(4)) Reg_B: pin names not known; wires that end beside it: A_Load[1], A_Load[0], Reset, Load, not_1_out, Clk_out, B_shift, B_Load[3], B_Load[2], B_Load[1], B_Load[0], Reg_B_p12, Reg_B_p13
  Multiplexer multiplexer_1 (.in0(Reg_B_p12), .in1(Reg_B_p13), .out(multiplexer_1_out), .sel(Sel));
  // Shift_Register #(.length(4)) Reg_C: pin names not known; wires that end beside it: Reset, 1'b0, 1'b1, Clk_out, multiplexer_1_out, 1'b0, 1'b0, 1'b0, 1'b0, Out_in_RegC[3], Out_in_RegC[2], Out_in_RegC[1], Out_in_RegC[0]

  // Notes on the sheet:
  //   Requires 4 clock cycles to obtain the sum output if we directly load the values
  //   Conditional operation using Shift registers
  //   S20210020303
  //   Pamidi Mohammad Ashraf
endmodule
