// Logisim project Test1.circ as structural Verilog: 2 circuits, main circuit Test
module main (
  input  a,
  input  b,
  input  S,
  output x
);

  wire and_1_out, not_1_out, test_1_outty;

  not not_1 (not_1_out, S);
  or or_1 (x, b, and_1_out);
  and and_1 (and_1_out, a, not_1_out);
  Test test_1 (.outty(test_1_outty));  // open: A, B, S
endmodule

module Test (
  input  A,
  input  B,
  input  S,
  output outty
);

  Multiplexer multiplexer_1 (.in0(A), .in1(B), .out(outty), .sel(S));
endmodule
