// Logisim project 4_bit_conditional_operator.circ as structural Verilog: 1 circuit, main circuit main
module main (
  input  [3:0] A,
  input  [3:0] B,
  input  En,
  input  Reset,
  input  Sel,
  output [3:0] O
);

  wire clk_out;
  wire [3:0] multiplexer_1_out, RegA_q, RegB_q;

  Clock clk (.out(clk_out));
  Register #(.width(4)) RegA (.D(A), .en(En), .clk(clk_out), .Q(RegA_q), .clr(Reset));
  Register #(.width(4)) RegB (.D(B), .en(En), .clk(clk_out), .Q(RegB_q), .clr(Reset));
  Multiplexer #(.width(4)) multiplexer_1 (.in0(RegA_q), .in1(RegB_q), .out(multiplexer_1_out), .sel(Sel));
  Register #(.width(4)) register_1 (.D(multiplexer_1_out), .en(En), .clk(clk_out), .Q(O), .clr(Reset));

  // Notes on the sheet:
  //   4 bit conditional operator
endmodule
