// Logisim project S20210020303_Assign1_Q2.circ as structural Verilog: 1 circuit, main circuit With_feedback
module With_feedback (
  input  Reset,
  input  Load,
  input  [3:0] A_Load,
  input  B_shift,
  input  [3:0] B_Load,
  output [3:0] Sum_in_RegA
);

  wire adder_1_cout, Clk_out, d_ff_1_q, not_1_out, Reg_A_p5, Reg_B_p14;

  Clock Clk (.out(Clk_out));
  not not_1 (not_1_out, Load);
  // Shift_Register #(.length(4)) Reg_A: pin names not known; wires that end beside it: Reset, Load, not_1_out, Clk_out, Reg_A_p5, A_Load[3], A_Load[2], Sum_in_RegA[3]
  // Shift_Register #(.length(4)) Reg_B: pin names not known; wires that end beside it: A_Load[1], A_Load[0], Reset, Load, not_1_out, Clk_out, B_shift, B_Load[3], B_Load[2], B_Load[1], B_Load[0], Sum_in_RegA[2], Sum_in_RegA[1], Reg_B_p14
  Adder #(.width(1)) adder_1 (.a(Sum_in_RegA[0]), .b(Reg_B_p14), .out(Reg_A_p5), .cin(d_ff_1_q), .cout(adder_1_cout));
  D_Flip_Flop d_ff_1 (.D(adder_1_cout), .clk(Clk_out), .Q(d_ff_1_q), .reset(Reset));  // open: Qn, preset

  // Notes on the sheet:
  //   4 bit Serial Adder using Shift registers
  //   Reg_A <- Reg_A + Reg_B
  //   Requires 4 clock cycles to obtain the sum if we directly load the values
  //   Pamidi Mohammad Ashraf
  //   S20210020303
endmodule
