// Logisim project S20210020303_Assign1_Q3.circ as structural Verilog: 1 circuit, main circuit Without_feedback
module Without_feedback (
  input  Reset,
  input  Load,
  input  A_Shift,
  input  [3:0] A_Load,
  input  B_shift,
  input  [3:0] B_Load,
  output [3:0] Sum_in_RegC
);

  wire adder_1_cout, adder_1_out, Clk_out, d_ff_1_q, not_1_out, Reg_B_p12, Reg_B_p13;

  Clock Clk (.out(Clk_out));
  not not_1 (not_1_out, Load);
  // Shift_Register #(.length(4)) Reg_A: pin names not known; wires that end beside it: Reset, Load, not_1_out, Clk_out, A_Shift, A_Load[3], A_Load[2]
  // Shift_Register #(.length(4)) Reg_B: pin names not known; wires that end beside it: A_Load[1], A_Load[0], Reset, Load, not_1_out, Clk_out, B_shift, B_Load[3], B_Load[2], B_Load[1], B_Load[0], Reg_B_p12, Reg_B_p13
  Adder #(.width(1)) adder_1 (.a(Reg_B_p12), .b(Reg_B_p13), .out(adder_1_out), .cin(d_ff_1_q), .cout(adder_1_cout));
  D_Flip_Flop d_ff_1 (.D(adder_1_cout), .clk(Clk_out), .Q(d_ff_1_q), .reset(Reset));  // open: Qn, preset
  // Shift_Register #(.length(4)) Reg_C: pin names not known; wires that end beside it: Reset, 1'b0, 1'b1, Clk_out, adder_1_out, 1'b0, 1'b0, 1'b0, 1'b0, Sum_in_RegC[3], Sum_in_RegC[2], Sum_in_RegC[1], Sum_in_RegC[0]

  // Notes on the sheet:
  //   4 bit Serial Adder using Shift registers
  //   Reg_C <- Reg_A + Reg_B
  //   Requires 4 clock cycles to obtain the sum if we directly load the values
  //   Pamidi Mohammad Ashraf
  //   S20210020303
endmodule
