// Logisim project Serial_Adder_2.circ as structural Verilog: 1 circuit, main circuit main
module main (
  input  [3:0] B,
  input  En,
  input  Reset,
  output [3:0] Carry,
  output [3:0] Sum
);

  wire clk_out;
  wire [0:0] adder_1_cout;
  wire [3:0] RegA_q, RegB_q;

  Clock clk (.out(clk_out));
  Register #(.width(4)) RegA (.D(Sum), .en(En), .clk(clk_out), .Q(RegA_q), .clr(Reset));
  Register #(.width(4)) RegB (.D(B), .en(En), .clk(clk_out), .Q(RegB_q), .clr(Reset));
  Adder #(.width(4)) adder_1 (.a(RegA_q), .b(RegB_q), .out(Sum), .cout(adder_1_cout[0]));  // open: cin
  Register #(.width(4)) register_1 (.D({3'b000, adder_1_cout[0]}), .en(En), .clk(clk_out), .Q(Carry), .clr(Reset));

  // Notes on the sheet:
  //   RegA <- RegA + RegB
endmodule
