// Logisim project Universal Shift Registers.circ as structural Verilog: 3 circuits, main circuit main
module main (
);


  // Notes on the sheet:
  //   <--------- Look at the different schematics
endmodule

module Bit_4 (
  input  Reset,
  input  Right_shift_Input,
  input  I3,
  input  I2,
  input  I1,
  input  I0,
  input  Left_shift_Input,
  input  [1:0] S1_S0,
  input  in_9,
  output P3,
  output P2,
  output P1,
  output P0
);

  wire CLK_out, multiplexer_1_out, multiplexer_2_out, multiplexer_3_out, multiplexer_4_out, or_1_out;

  LED led_1 (.in(I3));
  LED led_2 (.in(I2));
  LED led_3 (.in(I1));
  LED led_4 (.in(I0));
  Multiplexer #(.select(2)) multiplexer_1 (
    .in0(P3), .in1(Right_shift_Input), .in2(P2), .in3(I3), .out(multiplexer_1_out), .sel(S1_S0));
  Multiplexer #(.select(2)) multiplexer_2 (
    .in0(P2), .in1(P3), .in2(P1), .in3(I2), .out(multiplexer_2_out), .sel(S1_S0));
  Multiplexer #(.select(2)) multiplexer_3 (
    .in0(P1), .in1(P2), .in2(P0), .in3(I1), .out(multiplexer_3_out), .sel(S1_S0));
  Multiplexer #(.select(2)) multiplexer_4 (
    .in0(P0), .in1(P1), .in2(Left_shift_Input), .in3(I0), .out(multiplexer_4_out), .sel(S1_S0));
  or or_1 (or_1_out, CLK_out, in_9);
  D_Flip_Flop d_ff_1 (.D(multiplexer_1_out), .clk(or_1_out), .Q(P3), .reset(Reset));  // open: Qn, preset
  D_Flip_Flop d_ff_2 (.D(multiplexer_2_out), .clk(or_1_out), .Q(P2), .reset(Reset));  // open: Qn, preset
  D_Flip_Flop d_ff_3 (.D(multiplexer_3_out), .clk(or_1_out), .Q(P1), .reset(Reset));  // open: Qn, preset
  D_Flip_Flop d_ff_4 (.D(multiplexer_4_out), .clk(or_1_out), .Q(P0), .reset(Reset));  // open: Qn, preset
  Clock CLK (.out(CLK_out));
  LED led_5 (.in(P3));
  LED led_6 (.in(P2));
  LED led_7 (.in(P1));
  LED led_8 (.in(P0));

  // Notes on the sheet:
  //   4-bit Universal Shift Register
  //   ~ ~ ~ ~ ~ ~ ~ ~ ~ ~ ~ ~ ~ ~ ~ ~ ~ ~ ~ ~ ~ ~ ~ ~ ~ ~ ~ ~ ~ ~ ~ ~ ~ ~ ~ ~ ~ ~ ~ ~
  //   ~ ~ ~ ~ ~ ~ ~ ~ ~ ~ ~ ~ ~ ~ ~ ~ ~ ~ ~ ~ ~ ~ ~ ~ ~ ~ ~ ~ ~ ~ ~ ~ ~ ~ ~ ~ ~ ~ ~ ~
  //   |
  //   |
  //   |
  //   |
  //   |
  //   |
  //   |
  //   |
  //   |
  //   |
  //   |
  //   |
  //   |
  //   |
  //   |
  //   |
  //   |
  //   |
  //   |
  //   |
  //   |
  //   |
  //   |
  //   |
  //   |
  //   |
  //   |
  //   |
  //   |
  //   |
  //   |
  //   |
  //   |
  //   |
  //   |
  //   |
  //   |
  //   |
  //   |
  //   |
  //   |
  //   |
  //   |
  //   |
  //   |
  //   |
  //   |
  //   |
  //   |
  //   |
  //   |
  //   |
  //   |
  //   |
  //   |
  //   |
  //   |
  //   |
  //   |
  //   |
  //   |
  //   S1 S0
  //   _______
  //   _______
  //   00 - 
  //   01 - 
  //   10 - 
  //   11 - 
  //   ____________________________________
  //   __________________________________
  //   Outcome
  //   ___________
  //   ___________
  //   No Change
  //   Right Shift
  //   Left Shift
  //   Input
  //   __________________________________
  //   ____________________________________
  //   |
  //   |
  //   |
  //   |
  //   |
  //   |
  //   |
  //   |
  //   |
  //   |
  //   |
  //   |
  //   |
  //   |
  //   |
  //   |
  //   |
  //   |
  //   |
  //   |
  //   |
  //   |
  //   |
  //   |
  //   |
  //   |
  //   |
  //   |
  //   |
  //   |
  //   |
  //   |
  //   |
  //   |
  //   |
  //   |
  //   |
  //   |
  //   |
  //   |
  //   |
  //   |
  //   |
  //   |
  //   |
  //   |
  //   |
  //   |
  //   |
  //   |
  //   |
  //   |
  //   |
  //   |
  //   |
  //   |
  //   |
  //   |
  //   |
  //   |
  //   |
endmodule

module Bit_8 (
  input  [7:0] in_1,
  input  Left_Shift_Input,
  input  Right_shift_Input,
  input  [1:0] S1_S0,
  output P7,
  output P6,
  output P5,
  output P4,
  output P3,
  output P2,
  output P1,
  output P0
);

  wire CLk_out, Reset_out;

  Button Reset (.out(Reset_out));
  Clock CLk (.out(CLk_out));
  Bit_4 bit_4_1 (
    .Reset(Reset_out), .Right_shift_Input(P4), .I3(in_1[3]), .I2(in_1[2]), .I1(in_1[1]), .I0(in_1[0]),
    .Left_shift_Input(Left_Shift_Input), .S1_S0(S1_S0), .in_9(CLk_out), .P3(P3), .P2(P2), .P1(P1), .P0(P0));
  Bit_4 bit_4_2 (
    .Reset(Reset_out), .Right_shift_Input(Right_shift_Input), .I3(in_1[7]), .I2(in_1[6]), .I1(in_1[5]),
    .I0(in_1[4]), .Left_shift_Input(P3), .S1_S0(S1_S0), .in_9(CLk_out), .P3(P7), .P2(P6), .P1(P5), .P0(P4));
  LED led_1 (.in(P7));
  LED led_2 (.in(P6));
  LED led_3 (.in(P5));
  LED led_4 (.in(P4));
  LED led_5 (.in(P3));
  LED led_6 (.in(P2));
  LED led_7 (.in(P1));
  LED led_8 (.in(P0));

  // Notes on the sheet:
  //   I7 I6 I5 I4 I3 I2 I1 I0
  //   8-bit Universal Shift Register
  //   ~ ~ ~ ~ ~ ~ ~ ~ ~ ~ ~ ~ ~ ~ ~ ~ ~ ~ ~ ~ ~ ~ ~ ~ ~ ~ ~ ~ ~ ~ ~ ~ ~ ~ ~ ~ ~ ~ ~ ~
  //   ~ ~ ~ ~ ~ ~ ~ ~ ~ ~ ~ ~ ~ ~ ~ ~ ~ ~ ~ ~ ~ ~ ~ ~ ~ ~ ~ ~ ~ ~ ~ ~ ~ ~ ~ ~ ~ ~ ~ ~
  //   |
  //   |
  //   |
  //   |
  //   |
  //   |
  //   |
  //   |
  //   |
  //   |
  //   |
  //   |
  //   |
  //   |
  //   |
  //   |
  //   |
  //   |
  //   |
  //   |
  //   |
  //   |
  //   |
  //   |
  //   |
  //   |
  //   |
  //   |
  //   |
  //   |
  //   |
  //   |
  //   |
  //   |
  //   |
  //   |
  //   |
  //   |
  //   |
  //   |
  //   |
  //   |
  //   |
  //   |
  //   |
  //   |
  //   |
  //   |
  //   |
  //   |
  //   |
  //   |
  //   |
  //   |
  //   |
  //   |
  //   |
  //   |
  //   |
  //   |
  //   |
  //   S1 S0
  //   _______
  //   _______
  //   00 - 
  //   01 - 
  //   10 - 
  //   11 - 
  //   ____________________________________
  //   __________________________________
  //   Outcome
  //   ___________
  //   ___________
  //   No Change
  //   Right Shift
  //   Left Shift
  //   Input
  //   __________________________________
  //   ____________________________________
  //   |
  //   |
  //   |
  //   |
  //   |
  //   |
  //   |
  //   |
  //   |
  //   |
  //   |
  //   |
  //   |
  //   |
  //   |
  //   |
  //   |
  //   |
  //   |
  //   |
  //   |
  //   |
  //   |
  //   |
  //   |
  //   |
  //   |
  //   |
  //   |
  //   |
  //   |
  //   |
  //   |
  //   |
  //   |
  //   |
  //   |
  //   |
  //   |
  //   |
  //   |
  //   |
  //   |
  //   |
  //   |
  //   |
  //   |
  //   |
  //   |
  //   |
  //   |
  //   |
  //   |
  //   |
  //   |
  //   |
  //   |
  //   |
  //   |
  //   |
  //   |
endmodule
