// Logisim project BCD to 7-segment (Decimal).circ as structural Verilog
module BCD (
  input  A,
  input  B,
  input  C,
  input  D,
  output a_2,
  output b_2,
  output c_2,
  output d_2,
  output e,
  output f,
  output g
);

  wire and_1_out, and_2_out, and_3_out, and_4_out, and_5_out, and_6_out, and_7_out, and_8_out, and_9_out,
       and_10_out, and_11_out, and_12_out, and_13_out, and_14_out, and_15_out, and_16_out, and_17_out,
       and_18_out, and_19_out, and_20_out, and_21_out, not_1_out, not_2_out, not_3_out, not_4_out;

  not not_1 (not_1_out, A);
  not not_2 (not_2_out, B);
  not not_3 (not_3_out, C);
  not not_4 (not_4_out, D);
  and and_1 (and_1_out, B, not_3_out, D);
  and and_2 (and_2_out, not_2_out, not_4_out);
  and and_3 (and_3_out, not_1_out, not_2_out);
  and and_4 (and_4_out, not_3_out, not_4_out);
  and and_5 (and_5_out, C, D);
  or or_1 (c_2, A, B, not_3_out, D);
  and and_6 (and_6_out, not_2_out, not_4_out);
  and and_7 (and_7_out, B, not_3_out, D);
  and and_8 (and_8_out, not_1_out, not_2_out, C);
  and and_9 (and_9_out, A, C);
  and and_10 (and_10_out, A, B);
  and and_11 (and_11_out, C, not_4_out);
  and and_12 (and_12_out, not_2_out, not_4_out);
  and and_13 (and_13_out, A, B);
  and and_14 (and_14_out, A, C);
  and and_15 (and_15_out, C, not_4_out);
  and and_16 (and_16_out, not_3_out, not_4_out);
  and and_17 (and_17_out, B, not_3_out, D);
  and and_18 (and_18_out, B, C, not_4_out);
  and and_19 (and_19_out, B, not_3_out);
  and and_20 (and_20_out, C, not_4_out);
  and and_21 (and_21_out, not_1_out, not_2_out, C);
  or or_2 (a_2, A, C, and_1_out, and_2_out);
  or or_3 (b_2, and_3_out, A, and_4_out, and_5_out);
  or or_4 (d_2, and_6_out, and_7_out, and_8_out, and_9_out, and_10_out, and_11_out);
  or or_5 (e, and_12_out, and_13_out, and_14_out, and_15_out);
  or or_6 (f, A, and_16_out, and_17_out, and_18_out);
  or or_7 (g, A, and_19_out, and_20_out, and_21_out);
  LED led_1 (.in(a_2));
  LED led_2 (.in(b_2));
  LED led_3 (.in(c_2));
  LED led_4 (.in(d_2));
  LED led_5 (.in(e));
  LED led_6 (.in(f));
  LED led_7 (.in(g));
  _7_Segment_Display u_7_segment_display_1 (.g(g), .f(f), .a(a_2), .b(b_2), .e(e), .d(d_2), .c(c_2));  // open: dp

  // Notes on the sheet:
  //   Circuit Diagram
  //   ~~~~~~~~~~~~~~~~~~~~~~~~~~
  //   ~~~~~~~~~~~~~~~~~~~~~~~~~~
endmodule

module Segment7_decimal (
  input  [3:0] D
);

  wire bcd_1_a_2, bcd_1_b_2, bcd_1_c_2, bcd_1_d_2, bcd_1_e, bcd_1_f, bcd_1_g;

  BCD bcd_1 (
    .A(D[3]), .B(D[2]), .C(D[1]), .D(D[0]), .a_2(bcd_1_a_2), .b_2(bcd_1_b_2), .c_2(bcd_1_c_2),
    .d_2(bcd_1_d_2), .e(bcd_1_e), .f(bcd_1_f), .g(bcd_1_g));
  _7_Segment_Display u_7_segment_display_1 (
    .g(bcd_1_g), .f(bcd_1_f), .a(bcd_1_a_2), .b(bcd_1_b_2), .e(bcd_1_e), .d(bcd_1_d_2), .c(bcd_1_c_2));  // open: dp

  // Notes on the sheet:
  //   A
  //   B
  //   C
  //   B
  //   BCD to 7- Segment
  //   _______________________________
  //   _______________________________
  //   a
  //   c
  //   d
endmodule
