// Logisim project Circuit_1.circ as structural Verilog: 1 circuit, main circuit main
module main (
  input  B,
  input  A,
  input  C,
  output A_B_nA_C
);

  wire and_1_out, and_2_out, not_1_out;

  not not_1 (not_1_out, A);
  and and_1 (and_1_out, B, A);
  and and_2 (and_2_out, not_1_out, C);
  or or_1 (A_B_nA_C, and_1_out, and_2_out);

  // Notes on the sheet:
  //   = AB + ~AC
  //   Circuit 1
  //   A.B
  //   Y = AB+ ~AC+ ~ABC
  //   = AB + ~AC(1+B)
  //   ~A.C
endmodule
