// Logisim project Circuit_2.circ as structural Verilog: 1 circuit, main circuit main
module main (
  input  A,
  input  D,
  input  B,
  input  C,
  output out_5
);

  wire not_1_out, not_2_out, or_1_out, or_2_out, or_3_out;

  not not_1 (not_1_out, B);
  not not_2 (not_2_out, A);
  or or_1 (or_1_out, D, not_1_out);
  or or_2 (or_2_out, A, D);
  or or_3 (or_3_out, not_2_out, B, C);
  and and_1 (out_5, or_2_out, or_1_out, or_3_out);

  // Notes on the sheet:
  //   Circuit 2
  //   ~B+D
  //   ~A+B+C
  //   A+D
  //   (A+D)(~B+D)(~A+B+C)
endmodule
