// Logisim project Full_Adder.circ as structural Verilog: 1 circuit, main circuit main
module main (
  input  A,
  input  A_2,
  input  B,
  input  B_2,
  input  Cin,
  input  Cin_2,
  output Sum,
  output Sum_2,
  output Carry,
  output Carry_2
);

  wire and_1_out, and_2_out, and_3_out, and_4_out, and_5_out, and_6_out, not_1_out, not_2_out, xor_1_out,
       xor_2_out;

  not not_1 (not_1_out, A);
  xor xor_1 (xor_1_out, B, Cin);
  and and_1 (and_1_out, A, not_2_out);
  not not_2 (not_2_out, xor_1_out);
  and and_2 (and_2_out, not_1_out, xor_1_out);
  and and_3 (and_3_out, Cin, B);
  and and_4 (and_4_out, xor_1_out, A);
  or or_1 (Sum, and_1_out, and_2_out);
  or or_2 (Carry, and_3_out, and_4_out);
  xor xor_2 (xor_2_out, A_2, B_2);
  and and_5 (and_5_out, A_2, B_2);
  and and_6 (and_6_out, Cin_2, xor_2_out);
  xor xor_3 (Sum_2, xor_2_out, Cin_2);
  or or_3 (Carry_2, and_6_out, and_5_out);

  // Notes on the sheet:
  //   B'C+BC'
  //   A(BC+B'C')
  //   A'(B'C+BC')
  //   BC
  //   A(B'C+BC')
  //   A(BC+B'C') + A'(B'C+BC')
  //   A(B'C+BC') + BC
  //   =
  //   Full Adder
endmodule
