// Logisim project PISO.circ as structural Verilog: 1 circuit, main circuit main
module main (
  input  in_1,
  input  in_2,
  input  MSB,
  input  in_4,
  input  in_5,
  input  LSB,
  output out_7
);

  wire and_1_out, and_2_out, and_3_out, and_4_out, and_5_out, and_6_out, Clk_out, d_ff_1_q, d_ff_2_q,
       d_ff_3_q, not_1_out, or_1_out, or_2_out, or_3_out;

  not not_1 (not_1_out, in_1);
  Clock Clk (.out(Clk_out));
  and and_1 (and_1_out, in_5, not_1_out);
  and and_2 (and_2_out, in_1, d_ff_1_q);
  and and_3 (and_3_out, in_4, not_1_out);
  and and_4 (and_4_out, in_1, d_ff_2_q);
  and and_5 (and_5_out, MSB, not_1_out);
  and and_6 (and_6_out, in_1, d_ff_3_q);
  or or_1 (or_1_out, and_1_out, and_2_out);
  or or_2 (or_2_out, and_3_out, and_4_out);
  or or_3 (or_3_out, and_5_out, and_6_out);
  D_Flip_Flop d_ff_1 (.D(LSB), .clk(Clk_out), .Q(d_ff_1_q), .reset(in_2));  // open: Qn, preset
  D_Flip_Flop d_ff_2 (.D(or_1_out), .clk(Clk_out), .Q(d_ff_2_q), .reset(in_2));  // open: Qn, preset
  D_Flip_Flop d_ff_3 (.D(or_2_out), .clk(Clk_out), .Q(d_ff_3_q), .reset(in_2));  // open: Qn, preset
  D_Flip_Flop d_ff_4 (.D(or_3_out), .clk(Clk_out), .Q(out_7), .reset(in_2));  // open: Qn, preset
  LED led_1 (.in(out_7));

  // Notes on the sheet:
  //   Parallel IN serial out
endmodule
